// Logisim project s-mips.circ as structural Verilog: 30 circuits, main circuit S-MIPS Board
module S_MIPS_Board (
  input  DESHABILITAR_DISPATCHER,
  output halt
);

  wire button_1_out, CLK, CS, d_ff_1_q, LCLR, LoadRAM, LoadRAMOn, LW, R_R_W, R_W, ram_dispatcher_1_finished,
       RCS, Reset_out, RST, TTY_EN;
  wire [2:0] KDB;
  wire [3:0] LMask, Mask, ram_1_read_time, ram_1_write_time, RMask;
  wire [6:0] KDB_DATA, TTY_DATA;
  wire [15:0] Addr, LAddr, RAddr;
  wire [31:0] I0, I1, I2, I3, LData, ram_1_data_out_0, ram_1_data_out_1, ram_1_data_out_2, ram_1_data_out_3,
       RI0, RI1, RI2, RI3;

  TTY #(.rows(25), .cols(80)) tty_1 (.data(TTY_DATA), .clk(CLK), .we(TTY_EN), .clr(RST));
  not not_1 (LoadRAMOn, ram_dispatcher_1_finished);
  RAM_Dispatcher ram_dispatcher_1 (
    .WriteTime(ram_1_write_time), .Clock(CLK), .Data(LData), .Address(LAddr), .Mask(LMask),
    .Finished(ram_dispatcher_1_finished), .Write(LW), .CLR(LCLR));
  Keyboard #(.buflen(64)) keyboard_1 (.clk(CLK), .re(KDB[0]), .avail(KDB[2]), .data(KDB_DATA));  // open: clr
  RAM ram_1 (
    .Address(RAddr), .Data_Out_0(ram_1_data_out_0), .Data_Out_1(ram_1_data_out_1),
    .Data_Out_2(ram_1_data_out_2), .Data_Out_3(ram_1_data_out_3), .Data_In_0(RI0), .Data_In_1(RI1),
    .Data_In_2(RI2), .Data_In_3(RI3), .Mask(RMask), .nRead_Write(R_R_W), .Chip_Select(RCS),
    .Read_Time(ram_1_read_time), .Reset(button_1_out), .Write_Time(ram_1_write_time));
  // Probe on Addr
  Button button_1 (.out(button_1_out));
  D_Flip_Flop d_ff_1 (.clk(CLK), .D(1'b1), .Q(d_ff_1_q), .reset(Reset_out));  // open: Qn, preset, en
  Button Reset (.out(Reset_out));
  // Probe on ram_1_data_out_0
  S_MIPS s_mips_1 (
    .Kbd_Enable(KDB[0]), .Address(Addr), .Kbd_Clear(KDB[1]), .Kbd_Available(KDB[2]), .RAM_In_0(I0),
    .Kbd_ASCII_Data(KDB_DATA), .RAM_In_1(I1), .TTY_Enable(TTY_EN), .RAM_In_2(I2), .RAM_In_3(I3),
    .TTY_ASCII_Data(TTY_DATA), .Reset(RST), .RAM_Out_0(ram_1_data_out_0), .Clock(CLK),
    .RAM_Out_1(ram_1_data_out_1), .Stop(halt), .RAM_Out_2(ram_1_data_out_2), .RAM_Out_3(ram_1_data_out_3),
    .Mask(Mask), .Read_Time(ram_1_read_time), .Write_Time(ram_1_write_time), .nRead_Write(R_W),
    .Chip_Select(CS));
  D_Flip_Flop d_ff_2 (.clk(CLK), .D(d_ff_1_q), .Qn(LCLR), .reset(Reset_out));  // open: Q, preset, en
  // Probe on Mask
  or or_1 (RST, LCLR, LoadRAM);
  Clock clock_1 (.out(CLK));
  Multiplexer #(.width(32), .enable("false")) multiplexer_1 (.in0(I0), .in1(LData), .out(RI0), .sel(LoadRAM));
  Multiplexer #(.width(32), .enable("false")) multiplexer_2 (.in0(I1), .in1(LData), .out(RI1), .sel(LoadRAM));
  Multiplexer #(.width(32), .enable("false")) multiplexer_3 (.in0(I2), .in1(LData), .out(RI2), .sel(LoadRAM));
  Multiplexer #(.width(32), .enable("false")) multiplexer_4 (.in0(I3), .in1(LData), .out(RI3), .sel(LoadRAM));
  and and_1 (LoadRAM, ~DESHABILITAR_DISPATCHER, LoadRAMOn);  // AND_Gate
  Multiplexer #(.width(16), .enable("false")) multiplexer_5 (.in0(Addr), .in1(LAddr), .out(RAddr), .sel(LoadRAM));
  Multiplexer #(.width(4), .enable("false")) multiplexer_6 (.in0(Mask), .in1(LMask), .out(RMask), .sel(LoadRAM));
  Multiplexer #(.enable("false")) multiplexer_7 (.in0(CS), .in1(LW), .out(RCS), .sel(LoadRAM));
  Multiplexer #(.enable("false")) multiplexer_8 (.in0(R_W), .in1(LW), .out(R_R_W), .sel(LoadRAM));

  // Notes on the sheet:
  //   NO MODIFICAR
  //   Keyboard
endmodule

module RAM (
  input  [15:0] Address,
  input  [31:0] Data_In_0,
  input  [31:0] Data_In_1,
  input  [31:0] Data_In_2,
  input  [31:0] Data_In_3,
  input  [3:0] Mask,
  input  nRead_Write,
  input  Chip_Select,
  input  Reset,
  output [31:0] Data_Out_0,
  output [31:0] Data_Out_1,
  output [31:0] Data_Out_2,
  output [31:0] Data_Out_3,
  output [3:0] Read_Time,
  output [3:0] Write_Time
);

  wire and_2_out, and_3_out, and_4_out, and_5_out, and_6_out, and_7_out, and_8_out, and_9_out, Changed, CLK,
       comparator_2_eq, comparator_3_eq, comparator_4_eq, comparator_5_eq, comparator_6_eq, Count,
       demultiplexer_3_out0, Idle, Idle_q, Load, Load0, Load1, nand_1_out, or_1_out, or_2_out, or_3_out,
       or_4_out, or_5_out, or_6_out, or_7_out, or_8_out, or_9_out, or_10_out, Proc_q, Update_Mem, Zero_Time;
  wire [3:0] counter_1_q, multiplexer_1_out, subtractor_1_out;
  wire [31:0] register_1_q, register_2_q, register_3_q, register_4_q, register_5_q;

  // Probe on 4'b0011
  // Probe on 4'b0010
  Multiplexer #(.width(4), .enable("false")) multiplexer_1 (
    .in0(4'b0011), .in1(4'b0010), .out(multiplexer_1_out), .sel(nRead_Write));
  or or_1 (or_1_out, Idle, Update_Mem);
  or or_2 (or_2_out, ~Chip_Select, Reset);  // OR_Gate
  Subtractor #(.width(4)) subtractor_1 (.a(multiplexer_1_out), .b(4'b0010), .out(subtractor_1_out));  // open: bin, bout
  Demultiplexer #(.enable("false")) demultiplexer_1 (.out0(Idle), .out1(Load0), .in(Idle_q), .sel(Changed));
  D_Flip_Flop u_Idle (.clk(CLK), .D(or_1_out), .Q(Idle_q), .preset(or_2_out));  // open: Qn, en, reset
  // Probe on counter_1_q
  Counter #(.width(4), .max('hf)) counter_1 (
    .load(Load), .D(subtractor_1_out), .count(Count), .Q(counter_1_q), .clk(CLK), .clr(or_3_out));  // open: carry
  or or_3 (or_3_out, ~Chip_Select, Reset);  // OR_Gate
  Comparator #(.width(4), .mode("unsigned")) comparator_1 (
    .a(4'b0000), .b(counter_1_q), .eq(Zero_Time));  // open: gt, lt
  or or_4 (or_4_out, Count, Load0, Load1);
  Register #(.width(32)) register_1 (.D(Data_In_0), .en(Chip_Select), .Q(register_1_q), .clk(CLK), .clr(or_5_out));
  or or_5 (or_5_out, ~Chip_Select, Reset);  // OR_Gate
  Register #(.width(32)) register_2 (.D(Data_In_1), .en(Chip_Select), .Q(register_2_q), .clk(CLK), .clr(or_6_out));
  or or_6 (or_6_out, ~Chip_Select, Reset);  // OR_Gate
  Register #(.width(32)) register_3 (.D(Data_In_2), .en(Chip_Select), .Q(register_3_q), .clk(CLK), .clr(or_7_out));
  or or_7 (or_7_out, ~Chip_Select, Reset);  // OR_Gate
  Register #(.width(32)) register_4 (.D(Data_In_3), .en(Chip_Select), .Q(register_4_q), .clk(CLK), .clr(or_8_out));
  or or_8 (or_8_out, ~Chip_Select, Reset);  // OR_Gate
  Register #(.width(32)) register_5 (
    .D({{11{1'b1}}, nRead_Write, Mask, Address}), .en(Chip_Select), .Q(register_5_q), .clk(CLK),
    .clr(or_9_out));
  or or_9 (or_9_out, ~Chip_Select, Reset);  // OR_Gate
  D_Flip_Flop Proc (.clk(CLK), .D(or_4_out), .Q(Proc_q), .reset(or_10_out));  // open: Qn, preset, en
  or or_10 (or_10_out, ~Chip_Select, Reset);  // OR_Gate
  Demultiplexer #(.enable("false")) demultiplexer_2 (
    .out0(Count), .out1(Update_Mem), .in(demultiplexer_3_out0), .sel(Zero_Time));
  Demultiplexer #(.enable("false")) demultiplexer_3 (
    .out0(demultiplexer_3_out0), .out1(Load1), .in(Proc_q), .sel(Changed));
  Clock clock_1 (.out(CLK));
  Comparator #(.width(32)) comparator_2 (.a(register_1_q), .b(Data_In_0), .eq(comparator_2_eq));  // open: gt, lt
  Comparator #(.width(32)) comparator_3 (.a(register_2_q), .b(Data_In_1), .eq(comparator_3_eq));  // open: gt, lt
  Comparator #(.width(32)) comparator_4 (.a(register_3_q), .b(Data_In_2), .eq(comparator_4_eq));  // open: gt, lt
  Comparator #(.width(32)) comparator_5 (.a(register_4_q), .b(Data_In_3), .eq(comparator_5_eq));  // open: gt, lt
  Comparator #(.width(32)) comparator_6 (
    .a(register_5_q), .b({{11{1'b1}}, nRead_Write, Mask, Address}), .eq(comparator_6_eq));  // open: gt, lt
  nand nand_1 (nand_1_out, comparator_6_eq, comparator_2_eq, comparator_3_eq, comparator_4_eq, comparator_5_eq);
  and and_1 (Changed, nand_1_out, Chip_Select);
  or or_11 (Load, Count, Load1, Load0);
  and and_2 (and_2_out, Mask[0], Update_Mem, nRead_Write);
  and and_3 (and_3_out, Mask[1], Update_Mem, nRead_Write);
  and and_4 (and_4_out, Mask[2], Update_Mem, nRead_Write);
  and and_5 (and_5_out, Mask[3], Update_Mem, nRead_Write);
  RAM_part #(.addrWidth(16), .dataWidth(32), .bus("separate")) ram_1 (
    .addr(Address), .din(Data_In_0), .data(Data_Out_0), .str(and_2_out), .sel(Chip_Select), .clk(CLK),
    .ld(and_6_out), .clr(Reset));
  and and_6 (and_6_out, ~nRead_Write, Idle);  // AND_Gate
  RAM_part #(.addrWidth(16), .dataWidth(32), .bus("separate")) ram_2 (
    .addr(Address), .din(Data_In_1), .data(Data_Out_1), .str(and_3_out), .sel(Chip_Select), .clk(CLK),
    .ld(and_7_out), .clr(Reset));
  and and_7 (and_7_out, ~nRead_Write, Idle);  // AND_Gate
  RAM_part #(.addrWidth(16), .dataWidth(32), .bus("separate")) ram_3 (
    .addr(Address), .din(Data_In_2), .data(Data_Out_2), .str(and_4_out), .sel(Chip_Select), .clk(CLK),
    .ld(and_8_out), .clr(Reset));
  and and_8 (and_8_out, ~nRead_Write, Idle);  // AND_Gate
  RAM_part #(.addrWidth(16), .dataWidth(32), .bus("separate")) ram_4 (
    .addr(Address), .din(Data_In_3), .data(Data_Out_3), .str(and_5_out), .sel(Chip_Select), .clk(CLK),
    .ld(and_9_out), .clr(Reset));
  and and_9 (and_9_out, ~nRead_Write, Idle);  // AND_Gate

  assign Read_Time = 4'b0011;
  assign Write_Time = 4'b0010;

  // Other names for the same wires on the sheet: M0 = Mask[0]; M1 = Mask[1]; M2 = Mask[2]; M3 = Mask[3];
  //   RW = nRead_Write; CLR = Reset; CS = Chip_Select; Load2 = Count

  // Notes on the sheet:
  //   NO MODIFICAR
  //   excepto quizás los valores RT y WT
  //   BANK0
  //   BANK1
  //   BANK2
  //   BANK3
endmodule

module S_MIPS (
  input  Kbd_Available,
  input  [6:0] Kbd_ASCII_Data,
  input  [31:0] RAM_Out_0,
  input  [31:0] RAM_Out_1,
  input  Reset,
  input  [31:0] RAM_Out_2,
  input  Clock,
  input  [31:0] RAM_Out_3,
  input  [3:0] Read_Time,
  input  [3:0] Write_Time,
  output Kbd_Enable,
  output [15:0] Address,
  output Kbd_Clear,
  output TTY_Enable,
  output [6:0] TTY_ASCII_Data,
  output Stop,
  output [31:0] RAM_In_0,
  output [31:0] RAM_In_1,
  output [31:0] RAM_In_2,
  output [31:0] RAM_In_3,
  output [3:0] Mask,
  output nRead_Write,
  output Chip_Select
);

  // Probe on Mask
  Data_Path data_path_1 (
    .Kbd_Available(Kbd_Available), .Kbd_ASCII_Data(Kbd_ASCII_Data), .RAM_Out_0(RAM_Out_0), .Reset(Reset),
    .Clock(Clock), .RAM_Out_1(RAM_Out_1), .RAM_Out_2(RAM_Out_2), .RAM_Out_3(RAM_Out_3),
    .Read_Time(Read_Time), .Write_Time(Write_Time), .nRead_Write(nRead_Write), .Address(Address),
    .Chip_Select(Chip_Select), .Kbd_Enable(Kbd_Enable), .RAM_In_0(RAM_In_3), .Kbd_Clear(Kbd_Clear),
    .TTY_Enable(TTY_Enable), .Stop(Stop), .RAM_In_1(RAM_In_2), .TTY_ASCII_Data(TTY_ASCII_Data), .Mask(Mask),
    .RAM_In_2(RAM_In_1), .RAM_In_3(RAM_In_0));

  // Other names for the same wires on the sheet: CLK = Clock; CLR = Reset; CS = Chip_Select;
  //   KBD_AVAIL = Kbd_Available; KBD_CLR = Kbd_Clear; KBD_DATA[6:0] = Kbd_ASCII_Data; RAM_A[15:0] = Address;
  //   RAM_INPUT_0[31:0] = RAM_In_0; RAM_INPUT_1[31:0] = RAM_In_1; RAM_INPUT_2[31:0] = RAM_In_2;
  //   RAM_INPUT_3[31:0] = RAM_In_3; RAM_MASK[3:0] = Mask; RAM_OUTPUT_0[31:0] = RAM_Out_0;
  //   RAM_OUTPUT_1[31:0] = RAM_Out_1; RAM_OUTPUT_2[31:0] = RAM_Out_2; RAM_OUTPUT_3[31:0] = RAM_Out_3;
  //   RW = nRead_Write; TTY_DATA[6:0] = TTY_ASCII_Data

  // Notes on the sheet:
  //   RAM ADDRESS
  //   DATA FROM RAM
  //   DATA TO RAM
  //   DATA WRITE MASK
  //   RAM TIMING
  //   RAM CONTROL
  //   KEYBOARD
  //   TTY
  //   SEQUENCING
endmodule

module RAM_Dispatcher (
  input  [3:0] WriteTime,
  input  Clock,
  input  CLR,
  output [31:0] Data,
  output [15:0] Address,
  output [3:0] Mask,
  output Finished,
  output Write
);

  wire demultiplexer_2_out1, demultiplexer_3_out1, End, IDLE_q, IncAddr, Load, or_1_out, or_2_out, While_q,
       WriteEnd;
  wire [3:0] counter_1_q;
  wire [31:0] CurrentAddress_q;

  Counter #(.width(32), .max('hffffffff)) CurrentAddress (
    .count(IncAddr), .Q({CurrentAddress_q[31:18], Address, CurrentAddress_q[1:0]}), .clk(Clock), .clr(CLR));  // open: load, D, carry
  or or_1 (or_1_out, IncAddr, demultiplexer_3_out1, Finished);
  D_Flip_Flop IDLE (.clk(Clock), .D(or_1_out), .Q(IDLE_q), .preset(CLR));  // open: Qn, en, reset
  Demultiplexer #(.enable("false")) demultiplexer_1 (.out0(Load), .out1(Finished), .in(IDLE_q), .sel(End));
  D_Flip_Flop While (.clk(Clock), .D(or_2_out), .Q(While_q), .reset(CLR));  // open: Qn, preset, en
  or or_2 (or_2_out, Write, Load);
  RAM_part #(.addrWidth(18), .dataWidth(32)) ram_1 (
    .addr({Address, CurrentAddress_q[1:0]}), .data(Data), .clk(Clock));  // open: sel, ld, clr
  Demultiplexer #(.enable("false")) demultiplexer_2 (
    .out0(Write), .out1(demultiplexer_2_out1), .in(While_q), .sel(WriteEnd));
  Decoder #(.select(2)) decoder_1 (
    .out0(Mask[0]), .out1(Mask[1]), .out2(Mask[2]), .out3(Mask[3]), .sel(CurrentAddress_q[1:0]));  // open: en
  Demultiplexer #(.enable("false")) demultiplexer_3 (
    .out0(IncAddr), .out1(demultiplexer_3_out1), .in(demultiplexer_2_out1), .sel(End));
  Counter #(.width(4), .max('hf)) counter_1 (
    .load(Load), .D(WriteTime), .count(Write), .Q(counter_1_q), .clk(Clock));  // open: carry, clr
  Comparator #(.width(32)) comparator_1 (.a(Data), .b({32{1'b1}}), .eq(End));  // open: gt, lt
  Comparator #(.width(4)) comparator_2 (.a(4'b0000), .b(counter_1_q), .eq(WriteEnd));  // open: gt, lt

  // Other names for the same wires on the sheet: CLK = Clock; Count = Write; WT[3:0] = WriteTime
endmodule

// DATA PATH
module Data_Path (
  input  Kbd_Available,
  input  [6:0] Kbd_ASCII_Data,
  input  [31:0] RAM_Out_0,
  input  Reset,
  input  Clock,
  input  [31:0] RAM_Out_1,
  input  [31:0] RAM_Out_2,
  input  [31:0] RAM_Out_3,
  input  [3:0] Read_Time,
  input  [3:0] Write_Time,
  output nRead_Write,
  output [15:0] Address,
  output Chip_Select,
  output Kbd_Enable,
  output [31:0] RAM_In_0,
  output Kbd_Clear,
  output TTY_Enable,
  output Stop,
  output [31:0] RAM_In_1,
  output [6:0] TTY_ASCII_Data,
  output [3:0] Mask,
  output [31:0] RAM_In_2,
  output [31:0] RAM_In_3
);

  wire _1_Cycle, and_1_out, and_2_out, and_4_out, Cache_working, CS1, CS2, Data_Memory_Finish, Inmediate,
       Instruction_Memory_Finish, Memory_Save, Memory_Write, Mul_Div, or_1_out, or_2_out, or_3_out, or_5_out,
       or_6_out, or_7_out, PC_Enable, pop, push, Read_Write, Rnd, STOP_t, waiter_1_output, Write_Register;
  wire [1:0] Branch_Selector;
  wire [2:0] Branch_Code;
  wire [3:0] ALU_operation;
  wire [4:0] Destination_Address, Select_A, Select_B;
  wire [15:0] RAM_A_1, RAM_A_2;
  wire [27:0] PC;
  wire [31:0] ALU_result, Constant_K, Data_Input, data_memory_1_data_out, E0, E1,
       instruction_memory_cache_1_data_output, instruction_register_1_output, multiplexer_1_out,
       multiplexer_2_out, multiplexer_3_out, multiplier_1_out, Sp, Write_Data;
  wire [31:2] E2;
  wire [31:7] E3;

  Multiplier #(.width(32)) multiplier_1 (.a(Constant_K), .b(32'h4), .out(multiplier_1_out));  // open: cin, cout
  Multiplexer #(.select(2), .width(32), .enable("false")) multiplexer_1 (
    .in0(E0), .in1(E1), .in2({E2, 2'b00}), .in3({E3, TTY_ASCII_Data}), .out(multiplexer_1_out),
    .sel(Branch_Selector));
  Adder #(.width(32)) adder_1 (.a({E2[31:28], PC}), .b(32'h4), .out(E0));  // open: cin, cout
  Adder #(.width(32)) adder_2 (.a(E0), .b(multiplier_1_out), .out(E1));  // open: cin, cout
  PC pc_1 (.In(multiplexer_1_out), .Clock(Clock), .Enable(PC_Enable), .Clear(Reset), .Out({E2[31:28], PC}));
  or or_1 (or_1_out, Stop, STOP_t);
  D_Flip_Flop #(.trigger("falling")) d_ff_1 (.clk(Clock), .D(or_1_out), .Q(Stop));  // open: Qn, preset, en, reset
  and and_1 (and_1_out, Data_Memory_Finish, Memory_Write);
  Multiplexer #(.width(32), .enable("false")) multiplexer_2 (
    .in0({E2[31:28], PC}), .in1(ALU_result), .out(multiplexer_2_out), .sel(and_2_out));
  and and_2 (and_2_out, Data_Memory_Finish, Memory_Write);
  Instruction_Memory_Cache instruction_memory_cache_1 (
    .Reset(Reset), .Get(PC_Enable), .Address(multiplexer_2_out), .Read_Time(Read_Time), .RO0(RAM_Out_0),
    .RO2(RAM_Out_2), .RO1(RAM_Out_1), .RO3(RAM_Out_3), .Data_output(instruction_memory_cache_1_data_output),
    .Clock(Clock), .RAM_Address(RAM_A_1), .Chip_Select(CS1), .Ready(Instruction_Memory_Finish),
    .Cache_on_work(Cache_working), .Write_RAM(and_1_out), .Halt(STOP_t));
  Instruction_Register instruction_register_1 (
    .Data_in(instruction_memory_cache_1_data_output), .Clock(Clock), .Enable(Instruction_Memory_Finish),
    .Clear(or_2_out), .Output(instruction_register_1_output));
  or or_2 (or_2_out, Reset, waiter_1_output);
  Waiter waiter_1 (.PC_enable(PC_Enable), .Clock(Clock), .Output(waiter_1_output));
  Control_Unit control_unit_1 (
    .Clock(Clock), .IMR(Instruction_Memory_Finish), .DMR(Data_Memory_Finish), .II(_1_Cycle),
    .Chip_Select(Chip_Select), .Enable(PC_Enable), .Write_Register(Write_Register),
    .Cache_Working(Cache_working));
  Instruction_Decoder instruction_decoder_1 (
    .Instruction(instruction_register_1_output), .Select_A(Select_A), .Select_B(Select_B),
    .Constant_K(Constant_K), .Inmediate(Inmediate), .Mul_Div(Mul_Div), .Read_Write(Read_Write),
    .Write_Memory(Memory_Write), .Save_Memory(Memory_Save), .Branch_Code(Branch_Code),
    .Operation(ALU_operation), .Jump_Address(E2[27:2]), .Pop(pop), .Push(push),
    .Write_Address(Destination_Address), ._1_cycle_instruction(_1_Cycle), .STOP(STOP_t),
    .TTY_Enable(TTY_Enable), .Random(Rnd), .KBD(Kbd_Enable));
  or or_3 (or_3_out, ~Memory_Save, Data_Memory_Finish);  // OR_Gate
  and and_3 (Write_Register, Read_Write, or_3_out);
  and and_4 (and_4_out, pop, Data_Memory_Finish);
  or or_4 (Chip_Select, CS1, CS2);
  Register_File register_file_1 (
    .Read_Write(Write_Register), .Clock(Clock), .Data_Input(Data_Input),
    .Destination_Address(Destination_Address), .A_select(Select_A), .B_select(Select_B), .Pop(and_4_out),
    .Push(push), .A({E3, TTY_ASCII_Data}), .B(Write_Data), .Clear(Reset), .SP(Sp), .Random(Rnd),
    .KBD(Kbd_Enable), .Kbd_Available(Kbd_Available), .Kbd_ASCII_Data(Kbd_ASCII_Data),
    .RAM_FINISHED(Data_Memory_Finish));
  Multiplexer #(.width(32), .enable("false")) multiplexer_3 (
    .in0(Write_Data), .in1(Constant_K), .out(multiplexer_3_out), .sel(Inmediate));
  Branch_Control branch_control_1 (
    .A({E3, TTY_ASCII_Data}), .B(Write_Data), .Code(Branch_Code), .Selector(Branch_Selector));
  or or_5 (or_5_out, pop, push);
  or or_6 (or_6_out, Memory_Save, Memory_Write);
  ALU alu_1 (
    .A({E3, TTY_ASCII_Data}), .B(multiplexer_3_out), .Operation_Code(ALU_operation), .Mul_Div(Mul_Div),
    .Result(ALU_result), .Push_Pop(or_5_out), .SP(Sp));
  Multiplexer #(.width(16), .enable("false")) multiplexer_4 (
    .in0(RAM_A_1), .in1(RAM_A_2), .out(Address), .sel(or_6_out));
  or or_7 (or_7_out, Data_Memory_Finish, Reset);
  Data_Memory data_memory_1 (
    .Address(ALU_result), .Write_Data(Write_Data), .Write_Time(Write_Time), .Read_Time(Read_Time),
    .Data_Out(data_memory_1_data_out), .Clock(Clock), .Write_Entrance(Memory_Write),
    .Read_Entrance(Memory_Save), .Ram_Address(RAM_A_2), .Cls(or_7_out), .RO_0(RAM_Out_0), .RO_2(RAM_Out_2),
    .RO_1(RAM_Out_1), .RO_3(RAM_Out_3), .Data_To_RAM_0(RAM_In_0), .Data_To_RAM_2(RAM_In_2),
    .Data_To_RAM_1(RAM_In_1), .Data_To_RAM_3(RAM_In_3), .Chip_Select(CS2), .Write_RAM(nRead_Write),
    .Finished(Data_Memory_Finish), .Mask(Mask));  // open: RAM_read_finish
  Multiplexer #(.width(32), .enable("false")) multiplexer_5 (
    .in0(ALU_result), .in1(data_memory_1_data_out), .out(Data_Input), .sel(Memory_Save));
  // Probe on RAM_A_2

  assign Kbd_Clear = Reset;

  // Other names for the same wires on the sheet: CLK = Clock; CS = Chip_Select; Jump_Address[25:0] = E2[27:2];
  //   E3[6:0] = TTY_ASCII_Data; TTY_DATA[6:0] = TTY_ASCII_Data; KBD = Kbd_Enable; KBD_AVAIL = Kbd_Available;
  //   CLR = Reset; KBD_CLR = Reset; KBD_DATA[6:0] = Kbd_ASCII_Data; PC[31:28] = E2[31:28]; RAM_A[15:0] = Address;
  //   RAM_INPUT_0[31:0] = RAM_In_0; RAM_INPUT_1[31:0] = RAM_In_1; RAM_INPUT_2[31:0] = RAM_In_2;
  //   RAM_INPUT_3[31:0] = RAM_In_3; RAM_MASK[3:0] = Mask; RAM_OUTPUT_0[31:0] = RAM_Out_0;
  //   RAM_OUTPUT_1[31:0] = RAM_Out_1; RAM_OUTPUT_2[31:0] = RAM_Out_2; RAM_OUTPUT_3[31:0] = RAM_Out_3;
  //   RW = nRead_Write

  // Notes on the sheet:
  //   DATA FROM RAM
endmodule

module ALU (
  input  [31:0] A,
  input  [31:0] B,
  input  [3:0] Operation_Code,
  input  Mul_Div,
  input  [31:0] SP,
  input  Push_Pop,
  output [31:0] Result
);

  wire Sign_Enable;
  wire [3:0] divider_2_out;
  wire [31:0] a_complement, And, b_complement, Get_High, Get_Low, H, L, Nor, not_1_out, not_2_out, Or,
       Signed_Mul_Higher, Signed_Mul_Lower, Signed_Quotient, Signed_Remainder, slt, sltu, Sub_output,
       Sum_output, Unsigned_Mul_Higher, Unsigned_Mul_Lower, Unsigned_Quotient, Unsigned_Remainder, Xor;

  assign not_1_out = ~A;  // NOT_Gate not_1, 32 bits wide
  assign not_2_out = ~B;  // NOT_Gate not_2, 32 bits wide
  xor xor_1 (Sign_Enable, A[31], B[31]);
  Adder #(.width(32)) adder_1 (.a(not_1_out), .b(32'h1), .out(a_complement));  // open: cin, cout
  Adder #(.width(32)) adder_2 (.a(not_2_out), .b(32'h1), .out(b_complement));  // open: cin, cout
  Slt slt_1 (.A(A), .B(B), .Output(slt));
  Sltu sltu_1 (.A(A), .B(B), .Output(sltu));
  Adder #(.width(32)) adder_3 (.a(A), .b(B), .out(Sum_output), .cin(1'b0));  // open: cout
  Subtractor #(.width(32)) subtractor_1 (.a(A), .b(B), .out(Sub_output), .bin(1'b0));  // open: bout
  Multiplier #(.width(32)) multiplier_1 (
    .a(A), .b(B), .out(Unsigned_Mul_Lower), .cout(Unsigned_Mul_Higher));  // open: cin
  Divider #(.width(32)) divider_1 (.a(A), .b(B), .out(Unsigned_Quotient), .rem(Unsigned_Remainder));  // open: upper
  assign And = A & B;  // AND_Gate and_1, 32 bits wide
  assign Or = A | B;  // OR_Gate or_1, 32 bits wide
  assign Nor = ~(A | B);  // NOR_Gate nor_1, 32 bits wide
  assign Xor = A ^ B;  // XOR_Gate xor_2, 32 bits wide
  Signed_Mul signed_mul_1 (
    .Sign_Enable(Sign_Enable), .A(A), .B(B), .A_complement(a_complement), .B_complement(b_complement),
    .Final_Lower(Signed_Mul_Lower), .Final_Upper(Signed_Mul_Higher));
  Signed_Div signed_div_1 (
    .Sign_Enable(Sign_Enable), .A(A), .B(B), .A_complement(a_complement), .B_complement(b_complement),
    .FInal_Remainder(Signed_Remainder), .FInal_Quotient(Signed_Quotient));
  Multiplexer #(.select(2), .width(32), .enable("false")) multiplexer_1 (
    .in0(Unsigned_Mul_Higher), .in1(Signed_Mul_Higher), .in2(Unsigned_Remainder), .in3(Signed_Remainder),
    .out(H), .sel(divider_2_out[1:0]));
  Divider #(.width(4)) divider_2 (.a(Operation_Code), .b(4'b0010), .out(divider_2_out));  // open: upper, rem
  Register #(.width(32), .trigger("high")) High (.D(H), .en(Mul_Div), .Q(Get_High), .clk(1'b1));  // open: clr
  Multiplexer #(.select(4), .width(32), .disabled(0), .enable("false")) multiplexer_2 (
    .in0(Sum_output), .in1(Sub_output), .in2(Unsigned_Mul_Lower), .in3(Signed_Mul_Lower),
    .in4(Unsigned_Quotient), .in5(Signed_Quotient), .in6(And), .in7(Or), .in8(Nor), .in9(Xor), .in10(slt),
    .in11(sltu), .in12(Get_High), .in13(Get_Low), .in15({32{1'b0}}), .out(L), .sel(Operation_Code));  // open: in14
  Register #(.width(32), .trigger("high")) Low (.D(L), .en(Mul_Div), .Q(Get_Low), .clk(1'b1));  // open: clr
  // Probe on Operation_Code
  Multiplexer #(.width(32), .disabled(0), .enable("false")) multiplexer_3 (
    .in0(L), .in1(SP), .out(Result), .sel(Push_Pop));

  // Other names for the same wires on the sheet: a_sign = A[31]; b_sign = B[31]; Enable_High_Low = Mul_Div;
  //   Op_code[3:0] = Operation_Code
endmodule

// SIgn Mul
module Signed_Mul (
  input  Sign_Enable,
  input  [31:0] A,
  input  [31:0] B,
  input  [31:0] A_complement,
  input  [31:0] B_complement,
  output [31:0] Final_Lower,
  output [31:0] Final_Upper
);

  wire adder_1_cout;
  wire [31:0] adder_1_out, adder_2_out, Current_Lower, Current_Upper, multiplexer_1_out, multiplexer_2_out,
       not_1_out;

  Multiplexer #(.width(32), .enable("false")) multiplexer_1 (
    .in0(A), .in1(A_complement), .out(multiplexer_1_out), .sel(A[31]));
  Multiplexer #(.width(32), .enable("false")) multiplexer_2 (
    .in0(B), .in1(B_complement), .out(multiplexer_2_out), .sel(B[31]));
  assign not_1_out = ~Current_Lower;  // NOT_Gate not_1, 32 bits wide
  Adder #(.width(32)) adder_1 (.a(not_1_out), .b(32'h1), .out(adder_1_out), .cout(adder_1_cout));  // open: cin
  Adder #(.width(32)) adder_2 (.a(Current_Upper), .b(32'h1), .out(adder_2_out), .cin(adder_1_cout));  // open: cout
  Multiplier #(.width(32)) multiplier_1 (
    .a(multiplexer_1_out), .b(multiplexer_2_out), .out(Current_Lower), .cout(Current_Upper));  // open: cin
  Multiplexer #(.width(32), .disabled(0), .enable("false")) multiplexer_3 (
    .in0(Current_Lower), .in1(adder_1_out), .out(Final_Lower), .sel(Sign_Enable));
  Multiplexer #(.width(32), .disabled(0), .enable("false")) multiplexer_4 (
    .in0(Current_Upper), .in1(adder_2_out), .out(Final_Upper), .sel(Sign_Enable));

  // Other names for the same wires on the sheet: a_sign = A[31]; b_sign = B[31]
endmodule

// Sign Div
module Signed_Div (
  input  Sign_Enable,
  input  [31:0] A,
  input  [31:0] B,
  input  [31:0] A_complement,
  input  [31:0] B_complement,
  output [31:0] FInal_Remainder,
  output [31:0] FInal_Quotient
);

  wire [31:0] adder_1_out, Current_Quotient, multiplexer_1_out, multiplexer_2_out, not_1_out;

  Multiplexer #(.width(32), .enable("false")) multiplexer_1 (
    .in0(A), .in1(A_complement), .out(multiplexer_1_out), .sel(A[31]));
  Multiplexer #(.width(32), .enable("false")) multiplexer_2 (
    .in0(B), .in1(B_complement), .out(multiplexer_2_out), .sel(B[31]));
  assign not_1_out = ~Current_Quotient;  // NOT_Gate not_1, 32 bits wide
  Divider #(.width(32)) divider_1 (
    .a(multiplexer_1_out), .b(multiplexer_2_out), .out(Current_Quotient), .rem(FInal_Remainder));  // open: upper
  Adder #(.width(32)) adder_1 (.a(not_1_out), .b(32'h1), .out(adder_1_out));  // open: cin, cout
  Multiplexer #(.width(32), .enable("false")) multiplexer_3 (
    .in0(Current_Quotient), .in1(adder_1_out), .out(FInal_Quotient), .sel(Sign_Enable));

  // Other names for the same wires on the sheet: a_sign = A[31]; b_sign = B[31]
endmodule

module Branch_Control (
  input  [31:0] A,
  input  [31:0] B,
  input  [2:0] Code,
  output [1:0] Selector
);

  wire Beq, Bgtz, Blez, Bltz, Bnq, comparator_2_eq, decoder_1_out0, decoder_1_out1, decoder_1_out2,
       decoder_1_out3, decoder_1_out4, decoder_1_out5, decoder_1_out6;

  Decoder #(.select(3), .enable("false")) decoder_1 (
    .out0(decoder_1_out0), .out1(decoder_1_out1), .out2(decoder_1_out2), .out3(decoder_1_out3),
    .out4(decoder_1_out4), .out5(decoder_1_out5), .out6(decoder_1_out6), .sel(Code));  // open: out7
  Comparator #(.width(32)) comparator_1 (.a(A), .b(B), .eq(Beq));  // open: gt, lt
  not not_1 (Bnq, Beq);
  Comparator #(.width(32)) comparator_2 (.a(A), .b({32{1'b0}}), .gt(Bgtz), .eq(comparator_2_eq), .lt(Bltz));
  or or_1 (Blez, comparator_2_eq, Bltz);
  Branch_Selector branch_selector_1 (
    .Seq(decoder_1_out1), .Ceq(Beq), .Sne(decoder_1_out2), .Cne(Bnq), .Sletz(decoder_1_out3), .Clez(Blez),
    .Sgtz(decoder_1_out4), .Cgtz(Bgtz), .Sltz(decoder_1_out5), .Cltz(Bltz), .Sj(decoder_1_out0),
    .Sjr(decoder_1_out6), .Branch_Selector(Selector));
endmodule

module Branch_Code (
  input  Beq,
  input  Bne,
  input  Blez,
  input  Bgtz,
  input  Bltz,
  input  Jr,
  input  J,
  output [2:0] Output
);

  wire and_1_out, and_2_out, and_3_out, and_4_out, not_1_out, not_2_out, not_3_out, not_4_out, not_5_out,
       not_6_out, not_7_out, not_8_out, not_9_out, not_10_out, not_11_out, not_12_out, not_13_out,
       not_14_out, not_15_out, not_16_out, not_17_out, not_18_out, not_19_out, not_20_out, not_21_out,
       not_22_out, not_23_out, not_24_out, not_25_out, not_26_out;

  not not_1 (not_1_out, Beq);
  not not_2 (not_2_out, Bne);
  not not_3 (not_3_out, Blez);
  not not_4 (not_4_out, Bgtz);
  not not_5 (not_5_out, Bltz);
  not not_6 (not_6_out, J);
  not not_7 (not_7_out, Beq);
  not not_8 (not_8_out, Bne);
  not not_9 (not_9_out, Blez);
  not not_10 (not_10_out, Jr);
  not not_11 (not_11_out, J);
  not not_12 (not_12_out, Beq);
  not not_13 (not_13_out, Bne);
  not not_14 (not_14_out, Blez);
  not not_15 (not_15_out, Bgtz);
  not not_16 (not_16_out, Bltz);
  not not_17 (not_17_out, J);
  not not_18 (not_18_out, Beq);
  not not_19 (not_19_out, Bgtz);
  not not_20 (not_20_out, Bltz);
  not not_21 (not_21_out, Jr);
  not not_22 (not_22_out, J);
  not not_23 (not_23_out, Bne);
  not not_24 (not_24_out, Bgtz);
  not not_25 (not_25_out, Jr);
  not not_26 (not_26_out, J);
  and and_1 (and_1_out, not_1_out, not_2_out, not_3_out, not_4_out, not_5_out, not_6_out);
  and and_2 (and_2_out, not_7_out, not_8_out, not_9_out, not_10_out, not_11_out);
  and and_3 (and_3_out, not_12_out, not_13_out, not_14_out, not_15_out, not_16_out, not_17_out);
  and and_4 (and_4_out, not_18_out, not_19_out, not_20_out, not_21_out, not_22_out);
  and and_5 (Output[0], not_23_out, not_24_out, not_25_out, not_26_out);
  or or_1 (Output[2], and_1_out, and_2_out);
  or or_2 (Output[1], and_3_out, and_4_out);
endmodule

module Operation_Selector (
  input  S,
  input  R,
  input  Mu,
  input  Ms,
  input  Du,
  input  Ds,
  input  And,
  input  Or,
  input  Nor,
  input  Xor,
  input  Slt,
  input  Sltu,
  output [3:0] Operation
);

  wire not_1_out, not_2_out, not_3_out, not_4_out, not_5_out, not_6_out, not_7_out, not_8_out, not_9_out,
       not_10_out, not_11_out, not_12_out, not_13_out, not_14_out, not_15_out, not_16_out, not_17_out,
       not_18_out, not_19_out, not_20_out, not_21_out, not_22_out, not_23_out, not_24_out, not_25_out,
       not_26_out, not_27_out, not_28_out;

  not not_1 (not_1_out, S);
  not not_2 (not_2_out, R);
  not not_3 (not_3_out, Mu);
  not not_4 (not_4_out, Ms);
  not not_5 (not_5_out, Du);
  not not_6 (not_6_out, Ds);
  not not_7 (not_7_out, And);
  not not_8 (not_8_out, Or);
  not not_9 (not_9_out, S);
  not not_10 (not_10_out, R);
  not not_11 (not_11_out, Mu);
  not not_12 (not_12_out, Ms);
  not not_13 (not_13_out, Nor);
  not not_14 (not_14_out, Xor);
  not not_15 (not_15_out, Slt);
  not not_16 (not_16_out, Sltu);
  not not_17 (not_17_out, S);
  not not_18 (not_18_out, R);
  not not_19 (not_19_out, Du);
  not not_20 (not_20_out, Ds);
  not not_21 (not_21_out, Nor);
  not not_22 (not_22_out, Xor);
  not not_23 (not_23_out, S);
  not not_24 (not_24_out, Mu);
  not not_25 (not_25_out, Du);
  not not_26 (not_26_out, And);
  not not_27 (not_27_out, Nor);
  not not_28 (not_28_out, Slt);
  and and_1 (Operation[3], not_1_out, not_2_out, not_3_out, not_4_out, not_5_out, not_6_out, not_7_out, not_8_out);
  and and_2 (Operation[2], not_9_out, not_10_out, not_11_out, not_12_out, not_13_out, not_14_out, not_15_out, not_16_out);
  and and_3 (Operation[1], not_17_out, not_18_out, not_19_out, not_20_out, not_21_out, not_22_out);
  and and_4 (Operation[0], not_23_out, not_24_out, not_25_out, not_26_out, not_27_out, not_28_out);
endmodule

// Refister File
module Register_File (
  input  Clear,
  input  Read_Write,
  input  Clock,
  input  [31:0] Data_Input,
  input  [4:0] Destination_Address,
  input  [4:0] A_select,
  input  [4:0] B_select,
  input  Pop,
  input  Push,
  input  Random,
  input  KBD,
  input  Kbd_Available,
  input  [6:0] Kbd_ASCII_Data,
  input  RAM_FINISHED,
  output [31:0] A,
  output [31:0] B,
  output [31:0] SP
);

  wire and_1_out, and_2_out, and_3_out, comparator_1_eq, demultiplexer_1_out31, L0, L1, L2, L3, L4, L5, L6,
       L7, L8, L9, L10, L11, L12, L13, L14, L15, L16, L17, L18, L19, L20, L21, L22, L23, L24, L25, L26, L27,
       L28, L29, L30, L31, reader_writer_activator_1_output;
  wire [1:0] Code;
  wire [31:0] adder_1_out, E0, E1, E2, E3, E4, E5, E6, E7, E8, E9, E10, E11, E12, E13, E14, E15, E16, E17,
       E18, E19, E20, E21, E22, E23, E24, E25, E26, E27, E28, E29, E30, KBD_DATA, multiplexer_1_out,
       multiplexer_3_out, multiplexer_4_out, multiplexer_5_out, random_1_out, subtractor_1_out;

  and and_1 (and_1_out, KBD, Kbd_Available);
  and and_2 (and_2_out, KBD, ~Kbd_Available);  // AND_Gate
  Random #(.width(32)) random_1 (.clk(Clock), .next(1'b1), .out(random_1_out));  // open: clr
  assign KBD_DATA = {{25{1'b0}}, Kbd_ASCII_Data};  // Bit_Extender bit_extender_1
  or or_1 (Code[0], Random, and_2_out);
  or or_2 (Code[1], and_1_out, and_2_out);
  Multiplexer #(.select(2), .width(32), .disabled(0), .enable("false")) multiplexer_1 (
    .in0(Data_Input), .in1(random_1_out), .in2(KBD_DATA), .in3({32{1'b1}}), .out(multiplexer_1_out),
    .sel(Code));
  // Probe on Code
  Register #(.width(32)) register_1 (.D(multiplexer_1_out), .en(L0), .Q(E0), .clk(Clock), .clr(1'b1));
  Register #(.width(32)) register_2 (.D(multiplexer_1_out), .en(L1), .Q(E1), .clk(Clock), .clr(Clear));
  Register #(.width(32)) register_3 (.D(multiplexer_1_out), .en(L2), .Q(E2), .clk(Clock), .clr(Clear));
  Register #(.width(32)) register_4 (.D(multiplexer_1_out), .en(L3), .Q(E3), .clk(Clock), .clr(Clear));
  Register #(.width(32)) register_5 (.D(multiplexer_1_out), .en(L4), .Q(E4), .clk(Clock), .clr(Clear));
  Register #(.width(32)) register_6 (.D(multiplexer_1_out), .en(L5), .Q(E5), .clk(Clock), .clr(Clear));
  Register #(.width(32)) register_7 (.D(multiplexer_1_out), .en(L6), .Q(E6), .clk(Clock), .clr(Clear));
  Register #(.width(32)) register_8 (.D(multiplexer_1_out), .en(L7), .Q(E7), .clk(Clock), .clr(Clear));
  Multiplexer #(.select(5), .width(32), .enable("false")) multiplexer_2 (
    .in0(E0), .in1(E1), .in2(E2), .in3(E3), .in4(E4), .in5(E5), .in6(E6), .in7(E7), .in8(E8), .in9(E9),
    .in10(E10), .in11(E11), .in12(E12), .in13(E13), .in14(E14), .in15(E15), .in16(E16), .in17(E17),
    .in18(E18), .in19(E19), .in20(E20), .in21(E21), .in22(E22), .in23(E23), .in24(E24), .in25(E25),
    .in26(E26), .in27(E27), .in28(E28), .in29(E29), .in30(E30), .in31(SP), .out(A), .sel(A_select));
  Register #(.width(32)) register_9 (.D(multiplexer_1_out), .en(L8), .Q(E8), .clk(Clock), .clr(Clear));
  Register #(.width(32)) register_10 (.D(multiplexer_1_out), .en(L9), .Q(E9), .clk(Clock), .clr(Clear));
  Register #(.width(32)) register_11 (.D(multiplexer_1_out), .en(L10), .Q(E10), .clk(Clock), .clr(Clear));
  Register #(.width(32)) register_12 (.D(multiplexer_1_out), .en(L11), .Q(E11), .clk(Clock), .clr(Clear));
  Register #(.width(32)) register_13 (.D(multiplexer_1_out), .en(L12), .Q(E12), .clk(Clock), .clr(Clear));
  Register #(.width(32)) register_14 (.D(multiplexer_1_out), .en(L13), .Q(E13), .clk(Clock), .clr(Clear));
  Register #(.width(32)) register_15 (.D(multiplexer_1_out), .en(L14), .Q(E14), .clk(Clock), .clr(Clear));
  Register #(.width(32)) register_16 (.D(multiplexer_1_out), .en(L15), .Q(E15), .clk(Clock), .clr(Clear));
  Comparator #(.width(5), .mode("unsigned")) comparator_1 (
    .a(Destination_Address), .b({5{1'b1}}), .eq(comparator_1_eq));  // open: gt, lt
  Register #(.width(32)) register_17 (.D(multiplexer_1_out), .en(L16), .Q(E16), .clk(Clock), .clr(Clear));
  Register #(.width(32)) register_18 (.D(multiplexer_1_out), .en(L17), .Q(E17), .clk(Clock), .clr(Clear));
  Register #(.width(32)) register_19 (.D(multiplexer_1_out), .en(L18), .Q(E18), .clk(Clock), .clr(Clear));
  Register #(.width(32)) register_20 (.D(multiplexer_1_out), .en(L19), .Q(E19), .clk(Clock), .clr(Clear));
  Register #(.width(32)) register_21 (.D(multiplexer_1_out), .en(L20), .Q(E20), .clk(Clock), .clr(Clear));
  Register #(.width(32)) register_22 (.D(multiplexer_1_out), .en(L21), .Q(E21), .clk(Clock), .clr(Clear));
  Register #(.width(32)) register_23 (.D(multiplexer_1_out), .en(L22), .Q(E22), .clk(Clock), .clr(Clear));
  Register #(.width(32)) register_24 (.D(multiplexer_1_out), .en(L23), .Q(E23), .clk(Clock), .clr(Clear));
  Multiplexer #(.width(32), .enable("false")) multiplexer_3 (
    .in0(SP), .in1(Data_Input), .out(multiplexer_3_out), .sel(comparator_1_eq));
  Subtractor #(.width(32)) subtractor_1 (.a(SP), .b(32'h4), .out(subtractor_1_out));  // open: bin, bout
  Adder #(.width(32)) adder_1 (.a(multiplexer_3_out), .b(32'h4), .out(adder_1_out));  // open: cin, cout
  Register #(.width(32)) register_25 (.D(multiplexer_1_out), .en(L24), .Q(E24), .clk(Clock), .clr(Clear));
  Register #(.width(32)) register_26 (.D(multiplexer_1_out), .en(L25), .Q(E25), .clk(Clock), .clr(Clear));
  Register #(.width(32)) register_27 (.D(multiplexer_1_out), .en(L26), .Q(E26), .clk(Clock), .clr(Clear));
  Register #(.width(32)) register_28 (.D(multiplexer_1_out), .en(L27), .Q(E27), .clk(Clock), .clr(Clear));
  Register #(.width(32)) register_29 (.D(multiplexer_1_out), .en(L28), .Q(E28), .clk(Clock), .clr(Clear));
  Register #(.width(32)) register_30 (.D(multiplexer_1_out), .en(L29), .Q(E29), .clk(Clock), .clr(Clear));
  Register #(.width(32)) register_31 (.D(multiplexer_1_out), .en(L30), .Q(E30), .clk(Clock), .clr(Clear));
  Register #(.width(32)) register_32 (.D(multiplexer_5_out), .en(L31), .Q(SP), .clk(Clock));  // open: clr
  Multiplexer #(.select(2), .width(32), .enable("false")) multiplexer_4 (
    .in0(Data_Input), .in1(subtractor_1_out), .in2(adder_1_out), .out(multiplexer_4_out), .sel({Pop, Push}));  // open: in3
  Demultiplexer #(.select(5), .disabled(0)) demultiplexer_1 (
    .out0(L0), .out1(L1), .out2(L2), .out3(L3), .out4(L4), .out5(L5), .out6(L6), .out7(L7), .out8(L8),
    .out9(L9), .out10(L10), .out11(L11), .out12(L12), .out13(L13), .out14(L14), .out15(L15), .out16(L16),
    .out17(L17), .out18(L18), .out19(L19), .out20(L20), .out21(L21), .out22(L22), .out23(L23), .out24(L24),
    .out25(L25), .out26(L26), .out27(L27), .out28(L28), .out29(L29), .out30(L30),
    .out31(demultiplexer_1_out31), .in(1'b1), .sel(Destination_Address), .en(Read_Write));
  Multiplexer #(.width(32), .enable("false")) multiplexer_5 (
    .in0(multiplexer_4_out), .in1({32{1'b1}}), .out(multiplexer_5_out), .sel(Clear));
  Multiplexer #(.select(5), .width(32), .enable("false")) multiplexer_6 (
    .in0(E0), .in1(E1), .in2(E2), .in3(E3), .in4(E4), .in5(E5), .in6(E6), .in7(E7), .in8(E8), .in9(E9),
    .in10(E10), .in11(E11), .in12(E12), .in13(E13), .in14(E14), .in15(E15), .in16(E16), .in17(E17),
    .in18(E18), .in19(E19), .in20(E20), .in21(E21), .in22(E22), .in23(E23), .in24(E24), .in25(E25),
    .in26(E26), .in27(E27), .in28(E28), .in29(E29), .in30(E30), .in31(SP), .out(B), .sel(B_select));
  Reader_Writer_Activator reader_writer_activator_1 (
    .Clock(Clock), .Input(Push), .Output(reader_writer_activator_1_output));
  and and_3 (and_3_out, Pop, RAM_FINISHED);
  or or_3 (L31, demultiplexer_1_out31, Clear, and_3_out, reader_writer_activator_1_output);

  // Other names for the same wires on the sheet: a_selector[4:0] = A_select; b_selector[4:0] = B_select;
  //   datainput[31:0] = Data_Input; E31[31:0] = SP; KBD_AVAIL = Kbd_Available; Rnd = Random
endmodule

module Instruction_Decoder (
  input  [31:0] Instruction,
  output [4:0] Select_A,
  output [4:0] Select_B,
  output [31:0] Constant_K,
  output [4:0] Write_Address,
  output Inmediate,
  output Mul_Div,
  output STOP,
  output Read_Write,
  output TTY_Enable,
  output Random,
  output Write_Memory,
  output KBD,
  output Save_Memory,
  output [2:0] Branch_Code,
  output [3:0] Operation,
  output [25:0] Jump_Address,
  output Pop,
  output Push,
  output _1_cycle_instruction
);

  wire add, addi, \and , andi, Basic, beq, bgtz, blez, bltz, bne, comparator_1_eq, comparator_2_eq,
       comparator_3_eq, comparator_4_eq, comparator_22_eq, comparator_23_eq, comparator_24_eq,
       comparator_25_eq, comparator_27_eq, comparator_28_eq, comparator_29_eq, comparator_30_eq,
       comparator_31_eq, comparator_32_eq, comparator_33_eq, comparator_34_eq, comparator_35_eq,
       comparator_36_eq, comparator_37_eq, comparator_38_eq, div, divu, J, Jr, lw, mfh, mfl, mult, mulu,
       No_op, \nor , \or , or_2_out, or_3_out, or_4_out, or_5_out, or_6_out, or_7_out, or_8_out, or_14_out,
       ori, R, slt, slti, sltiu, sltu, Special, Stack, sub, sw, \xor , xori;
  wire [3:0] multiplexer_1_out, multiplexer_2_out, operation_selector_1_operation, or_10_out;
  wire [15:0] not_1_out;

  and and_1 (STOP, Special, comparator_1_eq);
  Comparator #(.width(6), .mode("unsigned")) comparator_1 (
    .a(Instruction[5:0]), .b({6{1'b1}}), .eq(comparator_1_eq));  // open: gt, lt
  and and_2 (TTY_Enable, Special, comparator_2_eq);
  Comparator #(.width(6), .mode("unsigned")) comparator_2 (
    .a(Instruction[5:0]), .b(6'b000001), .eq(comparator_2_eq));  // open: gt, lt
  and and_3 (Random, Special, comparator_3_eq);
  Comparator #(.width(6), .mode("unsigned")) comparator_3 (
    .a(Instruction[5:0]), .b(6'b000010), .eq(comparator_3_eq));  // open: gt, lt
  and and_4 (KBD, Special, comparator_4_eq);
  Comparator #(.width(6), .mode("unsigned")) comparator_4 (
    .a(Instruction[5:0]), .b(6'b000100), .eq(comparator_4_eq));  // open: gt, lt
  // Probe on Instruction[31:26]
  Comparator #(.width(6)) comparator_5 (.a({6{1'b0}}), .b(Instruction[31:26]), .eq(Basic));  // open: gt, lt
  Comparator #(.width(6)) comparator_6 (.a(6'b111000), .b(Instruction[31:26]), .eq(Stack));  // open: gt, lt
  Comparator #(.width(6)) comparator_7 (.a({6{1'b1}}), .b(Instruction[31:26]), .eq(Special));  // open: gt, lt
  Comparator #(.width(6)) comparator_8 (.a(6'b000010), .b(Instruction[31:26]), .eq(J));  // open: gt, lt
  Comparator #(.width(6)) comparator_9 (.a(6'b001000), .b(Instruction[31:26]), .eq(addi));  // open: gt, lt
  Comparator #(.width(6)) comparator_10 (.a(6'b001010), .b(Instruction[31:26]), .eq(slti));  // open: gt, lt
  Comparator #(.width(6)) comparator_11 (.a(6'b001011), .b(Instruction[31:26]), .eq(sltiu));  // open: gt, lt
  Comparator #(.width(6)) comparator_12 (.a(6'b001100), .b(Instruction[31:26]), .eq(andi));  // open: gt, lt
  Comparator #(.width(6)) comparator_13 (.a(6'b001101), .b(Instruction[31:26]), .eq(ori));  // open: gt, lt
  Comparator #(.width(6)) comparator_14 (.a(6'b001110), .b(Instruction[31:26]), .eq(xori));  // open: gt, lt
  Comparator #(.width(6)) comparator_15 (.a(6'b100011), .b(Instruction[31:26]), .eq(lw));  // open: gt, lt
  Comparator #(.width(6)) comparator_16 (.a(6'b101011), .b(Instruction[31:26]), .eq(sw));  // open: gt, lt
  Comparator #(.width(6)) comparator_17 (.a(6'b000100), .b(Instruction[31:26]), .eq(beq));  // open: gt, lt
  Comparator #(.width(6)) comparator_18 (.a(6'b000101), .b(Instruction[31:26]), .eq(bne));  // open: gt, lt
  Comparator #(.width(6)) comparator_19 (.a(6'b000110), .b(Instruction[31:26]), .eq(blez));  // open: gt, lt
  Comparator #(.width(6)) comparator_20 (.a(6'b000111), .b(Instruction[31:26]), .eq(bgtz));  // open: gt, lt
  Comparator #(.width(6)) comparator_21 (.a(6'b000001), .b(Instruction[31:26]), .eq(bltz));  // open: gt, lt
  or or_1 (R, Basic, Stack, Special);
  or or_2 (or_2_out, add, addi, Pop, sw, lw, Push);
  or or_3 (or_3_out, \and , andi);
  or or_4 (or_4_out, \or , ori);
  or or_5 (or_5_out, \xor , xori);
  or or_6 (or_6_out, slt, slti);
  or or_7 (or_7_out, sltu, sltiu);
  Operation_Selector operation_selector_1 (
    .S(or_2_out), .R(sub), .Mu(mulu), .Ms(mult), .Du(divu), .Ds(div), .And(or_3_out), .Or(or_4_out),
    .Nor(\nor ), .Xor(or_5_out), .Slt(or_6_out), .Sltu(or_7_out), .Operation(operation_selector_1_operation));
  Multiplexer #(.width(4), .enable("false")) multiplexer_1 (
    .in0(4'b0000), .in1(4'b1100), .out(multiplexer_1_out), .sel(mfh));
  Multiplexer #(.width(4), .enable("false")) multiplexer_2 (
    .in0(4'b0000), .in1(4'b1101), .out(multiplexer_2_out), .sel(mfl));
  or or_8 (or_8_out, mfh, mfl);
  or or_9 (Inmediate, addi, slti, sltiu, andi, ori, xori, lw, sw, beq, bne, blez, bgtz, bltz);
  Multiplexer #(.width(4), .enable("false")) multiplexer_3 (
    .in0(operation_selector_1_operation), .in1(or_10_out), .out(Operation), .sel(or_8_out));
  assign or_10_out = multiplexer_1_out | multiplexer_2_out;  // OR_Gate or_10, 4 bits wide
  assign not_1_out = ~Instruction[15:0];  // NOT_Gate not_1, 16 bits wide
  Adder #(.width(16)) adder_1 (.a(not_1_out), .b(16'h1));  // open: out, cin, cout
  Comparator #(.width(6)) comparator_22 (.a(6'b001000), .b(Instruction[5:0]), .eq(comparator_22_eq));  // open: gt, lt
  Comparator #(.width(6)) comparator_23 (.a(6'b010000), .b(Instruction[5:0]), .eq(comparator_23_eq));  // open: gt, lt
  Comparator #(.width(6)) comparator_24 (.a(6'b010010), .b(Instruction[5:0]), .eq(comparator_24_eq));  // open: gt, lt
  Comparator #(.width(6)) comparator_25 (.a({6{1'b0}}), .b(Instruction[5:0]), .eq(comparator_25_eq));  // open: gt, lt
  Comparator #(.width(6)) comparator_26 (.a(6'b100000), .b(Instruction[5:0]), .eq(add));  // open: gt, lt
  Comparator #(.width(6)) comparator_27 (.a(6'b100010), .b(Instruction[5:0]), .eq(comparator_27_eq));  // open: gt, lt
  Comparator #(.width(6)) comparator_28 (.a(6'b011000), .b(Instruction[5:0]), .eq(comparator_28_eq));  // open: gt, lt
  Comparator #(.width(6)) comparator_29 (.a(6'b011001), .b(Instruction[5:0]), .eq(comparator_29_eq));  // open: gt, lt
  Comparator #(.width(6)) comparator_30 (.a(6'b011010), .b(Instruction[5:0]), .eq(comparator_30_eq));  // open: gt, lt
  Comparator #(.width(6)) comparator_31 (.a(6'b011011), .b(Instruction[5:0]), .eq(comparator_31_eq));  // open: gt, lt
  Comparator #(.width(6)) comparator_32 (.a(6'b101010), .b(Instruction[5:0]), .eq(comparator_32_eq));  // open: gt, lt
  Comparator #(.width(6)) comparator_33 (.a(6'b101011), .b(Instruction[5:0]), .eq(comparator_33_eq));  // open: gt, lt
  Comparator #(.width(6)) comparator_34 (.a(6'b100100), .b(Instruction[5:0]), .eq(comparator_34_eq));  // open: gt, lt
  Comparator #(.width(6)) comparator_35 (.a(6'b100101), .b(Instruction[5:0]), .eq(comparator_35_eq));  // open: gt, lt
  Comparator #(.width(6)) comparator_36 (.a(6'b100111), .b(Instruction[5:0]), .eq(comparator_36_eq));  // open: gt, lt
  Comparator #(.width(6)) comparator_37 (.a(6'b101000), .b(Instruction[5:0]), .eq(comparator_37_eq));  // open: gt, lt
  Comparator #(.width(6)) comparator_38 (.a(6'b000001), .b(Instruction[5:0]), .eq(comparator_38_eq));  // open: gt, lt
  and and_5 (Jr, comparator_22_eq, R);
  and and_6 (mfh, comparator_23_eq, R);
  and and_7 (No_op, Basic, comparator_25_eq);
  and and_8 (Pop, comparator_25_eq, Stack);
  and and_9 (sub, comparator_27_eq, R);
  and and_10 (mult, comparator_28_eq, R);
  and and_11 (mulu, comparator_29_eq, R);
  and and_12 (div, comparator_30_eq, R);
  and and_13 (divu, comparator_31_eq, R);
  and and_14 (slt, comparator_32_eq, R);
  and and_15 (sltu, comparator_33_eq, R);
  and and_16 (\and , comparator_34_eq, R);
  and and_17 (\or , comparator_35_eq, R);
  and and_18 (\nor , comparator_36_eq, R);
  and and_19 (\xor , comparator_37_eq, R);
  and and_20 (Push, comparator_38_eq, Stack);
  Multiplexer #(.width(5), .enable("false")) multiplexer_4 (
    .in0(Instruction[25:21]), .in1(Instruction[20:16]), .out(Select_A), .sel(Push));
  Multiplexer #(.width(5), .enable("false")) multiplexer_5 (
    .in0(Instruction[20:16]), .in1(Instruction[25:21]), .out(Select_B), .sel(Push));
  and and_21 (mfl, R, comparator_24_eq);
  or or_11 (Write_Memory, Push, sw);
  or or_12 (Save_Memory, Pop, lw);
  Multiplexer #(.width(5), .enable("false")) multiplexer_6 (
    .in0(Instruction[15:11]), .in1(Instruction[20:16]), .out(Write_Address), .sel(Inmediate));
  or or_13 (Mul_Div, mult, mulu, div, divu);
  Branch_Code branch_code_1 (
    .Beq(beq), .Bne(bne), .Blez(blez), .Bgtz(bgtz), .Bltz(bltz), .Jr(Jr), .J(J), .Output(Branch_Code));
  nor nor_1 (_1_cycle_instruction, lw, Stack, sw);
  or or_14 (or_14_out, mfl, mfh);
  or or_15 (Read_Write, slti, add, Pop, sub, slt, sltu, \and , \or , \nor , \xor , andi, ori, xori, lw, sltiu, addi, or_14_out, Random);

  assign Constant_K = {{17{Instruction[15]}}, Instruction[14:0]};
  assign Jump_Address = Instruction[25:0];

  // Other names for the same wires on the sheet: I = Inmediate; Jump_Destination[25:0] = Instruction[25:0];
  //   Remainder[25:0] = Instruction[25:0]; Rt[4:0] = Instruction[20:16]; Rs[4:0] = Instruction[25:21];
  //   OpCode[5:0] = Instruction[31:26]; Constant[15:0] = Instruction[15:0]; Func_Code[5:0] = Instruction[5:0];
  //   offset[31:0] = {{17{Instruction[15]}}, Instruction[14:0]}; Rd[4:0] = Instruction[15:11]; rnd = Random
endmodule

// Branch Selelctor
module Branch_Selector (
  input  Seq,
  input  Ceq,
  input  Sne,
  input  Cne,
  input  Sletz,
  input  Clez,
  input  Sgtz,
  input  Cgtz,
  input  Sltz,
  input  Cltz,
  input  Sj,
  input  Sjr,
  output [1:0] Branch_Selector
);

  wire and_1_out, and_2_out, and_3_out, and_4_out, and_5_out, or_1_out;

  and and_1 (and_1_out, Seq, Ceq);
  and and_2 (and_2_out, Sne, Cne);
  and and_3 (and_3_out, Sletz, Clez);
  and and_4 (and_4_out, Sgtz, Cgtz);
  and and_5 (and_5_out, Sltz, Cltz);
  or or_1 (or_1_out, and_1_out, and_2_out, and_3_out, and_4_out, and_5_out);
  or or_2 (Branch_Selector[0], or_1_out, Sjr);
  or or_3 (Branch_Selector[1], Sjr, Sj);
endmodule

module Slt (
  input  [31:0] A,
  input  [31:0] B,
  output [31:0] Output
);

  wire comparator_1_lt;

  Comparator #(.width(32)) comparator_1 (.a(A), .b(B), .lt(comparator_1_lt));  // open: gt, eq
  Multiplexer #(.enable("false")) multiplexer_1 (.in0(1'b0), .in1(1'b1), .out(Output[0]), .sel(comparator_1_lt));

  assign Output[31:1] = {31{1'b0}};
endmodule

module Sltu (
  input  [31:0] A,
  input  [31:0] B,
  output [31:0] Output
);

  wire comparator_1_lt;

  Comparator #(.width(32), .mode("unsigned")) comparator_1 (.a(A), .b(B), .lt(comparator_1_lt));  // open: gt, eq
  Multiplexer #(.enable("false")) multiplexer_1 (.in0(1'b0), .in1(1'b1), .out(Output[0]), .sel(comparator_1_lt));

  assign Output[31:1] = {31{1'b0}};
endmodule

module Address_Separator (
  input  [31:0] Address,
  output [1:0] Output_selector,
  output [3:0] Mask,
  output [15:0] RAM_Address
);

  Demultiplexer #(.select(2), .enable("false")) demultiplexer_1 (
    .out0(Mask[0]), .out1(Mask[1]), .out2(Mask[2]), .out3(Mask[3]), .in(1'b1), .sel(Address[3:2]));

  assign Output_selector = Address[3:2];
  assign RAM_Address = Address[19:4];
endmodule

module Data_Memory (
  input  Clock,
  input  Write_Entrance,
  input  Read_Entrance,
  input  Cls,
  input  [31:0] Address,
  input  [31:0] Write_Data,
  input  [3:0] Write_Time,
  input  [3:0] Read_Time,
  input  [31:0] RO_0,
  input  [31:0] RO_2,
  input  [31:0] RO_1,
  input  [31:0] RO_3,
  output Write_RAM,
  output Chip_Select,
  output [31:0] Data_Out,
  output Finished,
  output [31:0] Data_To_RAM_0,
  output [31:0] Data_To_RAM_2,
  output [31:0] Data_To_RAM_1,
  output [31:0] Data_To_RAM_3,
  output [15:0] Ram_Address,
  output [3:0] Mask,
  output RAM_read_finish
);

  wire or_2_out, RCS, RE, Ready_Write, timer_1_ready, WCS1, WCS2, WE;

  Reader_Writer_Activator Write_Activator (.Clock(Clock), .Input(Write_Entrance), .Output(WE));
  Reader_Writer_Activator Read_Activator (.Clock(Clock), .Input(Read_Entrance), .Output(RE));
  Instruction_Memory instruction_memory_1 (
    .Address(Address), .Read_Time(Read_Time), .RO0(RO_0), .RO2(RO_2), .RO1(RO_1), .RO3(RO_3),
    .Data_output(Data_Out), .Clock(Clock), .RAM_Address(Ram_Address), .Chip_Select(RCS), .Get(RE),
    .Reset(Cls), .Ready(RAM_read_finish), .Mask(Mask));
  Inversor Inversor (.Data_In(Write_Data), .Data_Out(Data_To_RAM_0));
  or or_1 (Write_RAM, WCS1, WCS2);
  or or_2 (or_2_out, WE, timer_1_ready);
  D_Flip_Flop #(.trigger("falling")) d_ff_1 (.clk(Clock), .D(WE), .Q(WCS1), .en(or_2_out));  // open: Qn, preset, reset
  Timer timer_1 (.Time(Write_Time), .Clock(Clock), .Reset(Cls), .Start(WCS1), .Ready(timer_1_ready));
  or or_3 (Chip_Select, RCS, Write_RAM);
  D_Flip_Flop #(.trigger("falling")) d_ff_2 (
    .clk(Clock), .D(timer_1_ready), .Q(WCS2), .reset(Ready_Write));  // open: Qn, preset, en
  or or_4 (Finished, RAM_read_finish, Ready_Write);
  D_Flip_Flop #(.trigger("falling")) d_ff_3 (.clk(Clock), .D(WCS2), .Q(Ready_Write));  // open: Qn, preset, en, reset

  assign Data_To_RAM_1 = Data_To_RAM_0;
  assign Data_To_RAM_2 = Data_To_RAM_0;
  assign Data_To_RAM_3 = Data_To_RAM_0;

  // Other names for the same wires on the sheet: Clck = Clock; Data[31:0] = Write_Data; RA[15:0] = Ram_Address;
  //   RAM_OUTPUT_0[31:0] = RO_0; RAM_OUTPUT_1[31:0] = RO_1; RAM_OUTPUT_2[31:0] = RO_2; RAM_OUTPUT_3[31:0] = RO_3;
  //   RE_first = Read_Entrance; Ready_Read = RAM_read_finish; RT[3:0] = Read_Time; WCS = Write_RAM;
  //   WE_first = Write_Entrance; WT[3:0] = Write_Time
endmodule

module Instruction_Memory (
  input  Clock,
  input  Reset,
  input  Get,
  input  [31:0] Address,
  input  [3:0] Read_Time,
  input  [31:0] RO0,
  input  [31:0] RO2,
  input  [31:0] RO1,
  input  [31:0] RO3,
  output Chip_Select,
  output Ready,
  output [15:0] RAM_Address,
  output [31:0] Data_output,
  output [3:0] Mask
);

  wire CS1, CS2, or_1_out, timer_1_ready;
  wire [1:0] Output_Selector;
  wire [31:0] multiplexer_1_out, RAM_OUTPUT_0, RAM_OUTPUT_1, RAM_OUTPUT_2, RAM_OUTPUT_3;

  Register #(.width(32)) register_1 (.D(RO0), .en(CS2), .Q(RAM_OUTPUT_0), .clk(Clock));  // open: clr
  Register #(.width(32)) register_2 (.D(RO1), .en(CS2), .Q(RAM_OUTPUT_1), .clk(Clock));  // open: clr
  Address_Separator Address_Separator (
    .Address(Address), .Output_selector(Output_Selector), .Mask(Mask), .RAM_Address(RAM_Address));
  Register #(.width(32)) register_3 (.D(RO2), .en(CS2), .Q(RAM_OUTPUT_2), .clk(Clock));  // open: clr
  Register #(.width(32)) register_4 (.D(RO3), .en(CS2), .Q(RAM_OUTPUT_3), .clk(Clock));  // open: clr
  or or_1 (or_1_out, Get, timer_1_ready);
  or or_2 (Chip_Select, CS1, CS2);
  D_Flip_Flop #(.trigger("falling")) d_ff_1 (.clk(Clock), .D(Get), .Q(CS1), .en(or_1_out));  // open: Qn, preset, reset
  Timer timer_1 (.Time(Read_Time), .Clock(Clock), .Reset(Reset), .Start(CS1), .Ready(timer_1_ready));
  D_Flip_Flop #(.trigger("falling")) d_ff_2 (
    .clk(Clock), .D(timer_1_ready), .Q(CS2), .reset(Ready));  // open: Qn, preset, en
  Inversor Inversor (.Data_In(multiplexer_1_out), .Data_Out(Data_output));
  Multiplexer #(.select(2), .width(32), .disabled(0), .enable("false")) multiplexer_1 (
    .in0(RAM_OUTPUT_0), .in1(RAM_OUTPUT_1), .in2(RAM_OUTPUT_2), .in3(RAM_OUTPUT_3), .out(multiplexer_1_out),
    .sel(Output_Selector));
  D_Flip_Flop #(.trigger("falling")) d_ff_3 (.clk(Clock), .D(CS2), .Q(Ready));  // open: Qn, preset, en, reset

  // Other names for the same wires on the sheet: Clck = Clock
endmodule

module Timer (
  input  [3:0] Time,
  input  Clock,
  input  Start,
  input  Reset,
  output Ready
);

  wire or_1_out;
  wire [3:0] counter_1_q;

  Counter #(.width(4), .max('hf)) counter_1 (
    .Q(counter_1_q), .clk(Clock), .clr(or_1_out));  // open: load, D, count, carry
  or or_1 (or_1_out, Reset, ~Start);  // OR_Gate
  Comparator #(.width(4), .mode("unsigned")) comparator_1 (.a(Time), .b(counter_1_q), .lt(Ready));  // open: gt, eq
endmodule

module Control_Unit (
  input  Clock,
  input  IMR,
  input  DMR,
  input  II,
  input  Chip_Select,
  input  Write_Register,
  input  Cache_Working,
  output Enable
);

  wire d_ff_1_q, d_ff_2_qn, or_1_out, or_2_out, Starter_start;

  D_Flip_Flop #(.trigger("falling")) d_ff_1 (
    .clk(Clock), .D(Write_Register), .Q(d_ff_1_q));  // open: Qn, preset, en, reset
  starter Starter (.Clock(Clock), .Start(Starter_start));
  or or_1 (or_1_out, DMR, d_ff_1_q, II);
  or or_2 (or_2_out, or_1_out, Starter_start);
  D_Flip_Flop #(.trigger("falling")) d_ff_2 (.clk(Clock), .D(Enable), .Qn(d_ff_2_qn));  // open: Q, preset, en, reset
  and and_1 (Enable, d_ff_2_qn, ~Chip_Select, ~IMR, or_2_out, ~Cache_Working);  // AND_Gate

  // Other names for the same wires on the sheet: CS = Chip_Select
endmodule

module Inversor (
  input  [31:0] Data_In,
  output [31:0] Data_Out
);


  assign Data_Out = {Data_In[7:0], Data_In[15:8], Data_In[23:16], Data_In[31:24]};
endmodule

module starter (
  input  Clock,
  output Start
);

  wire d_ff_1_q, d_ff_1_qn;

  D_Flip_Flop #(.trigger("falling")) d_ff_1 (
    .clk(Clock), .D(d_ff_1_qn), .Q(d_ff_1_q), .Qn(d_ff_1_qn), .en(d_ff_1_qn));  // open: preset, reset
  D_Flip_Flop d_ff_2 (.clk(Clock), .D(d_ff_1_q), .Qn(Start), .en(Start));  // open: Q, preset, reset
endmodule

module PC (
  input  Clock,
  input  Enable,
  input  Clear,
  input  [31:0] In,
  output [31:0] Out
);

  wire starter_1_start;
  wire [31:0] multiplexer_1_out;

  starter starter_1 (.Clock(Clock), .Start(starter_1_start));
  Multiplexer #(.width(32), .enable("false")) multiplexer_1 (
    .in0(In), .in1({32{1'b0}}), .out(multiplexer_1_out), .sel(starter_1_start));
  Register #(.width(32)) register_1 (.D(multiplexer_1_out), .en(Enable), .Q(Out), .clk(Clock), .clr(Clear));

  // Other names for the same wires on the sheet: Clck = Clock; Clr = Clear; En = Enable
endmodule

module Waiter (
  input  PC_enable,
  input  Clock,
  output Output
);

  D_Flip_Flop #(.trigger("falling")) d_ff_1 (.clk(Clock), .D(PC_enable), .Q(Output));  // open: Qn, preset, en, reset
endmodule

// IR
module Instruction_Register (
  input  [31:0] Data_in,
  input  Clock,
  input  Enable,
  input  Clear,
  output [31:0] Output
);

  Register #(.width(32)) register_1 (.D(Data_in), .en(Enable), .Q(Output), .clk(Clock), .clr(Clear));
endmodule

module Reader_Writer_Activator (
  input  Clock,
  input  Input,
  output Output
);

  wire and_1_out, and_2_out, and_3_out, d_ff_1_q, d_ff_1_qn, d_ff_2_q, or_1_out;

  and and_1 (and_1_out, ~d_ff_1_q, d_ff_2_q, Input);  // AND_Gate
  and and_2 (and_2_out, d_ff_1_q, ~d_ff_2_q, Input);  // AND_Gate
  or or_1 (or_1_out, and_1_out, and_2_out);
  and and_3 (and_3_out, ~d_ff_1_q, ~d_ff_2_q, Input);  // AND_Gate
  D_Flip_Flop #(.trigger("falling")) d_ff_1 (
    .clk(Clock), .D(or_1_out), .Q(d_ff_1_q), .Qn(d_ff_1_qn));  // open: preset, en, reset
  D_Flip_Flop #(.trigger("falling")) d_ff_2 (.clk(Clock), .D(and_3_out), .Q(d_ff_2_q));  // open: Qn, preset, en, reset
  and and_4 (Output, d_ff_1_qn, d_ff_2_q);

  // Other names for the same wires on the sheet: Clck = Clock
endmodule

// Valid
module Bit_de_validez (
  input  Clock,
  input  In,
  input  Clear,
  output Output
);

  wire and_1_out, d_ff_1_qn;

  and and_1 (and_1_out, In, d_ff_1_qn);
  D_Flip_Flop #(.trigger("falling")) d_ff_1 (
    .clk(Clock), .D(and_1_out), .Q(Output), .Qn(d_ff_1_qn), .en(d_ff_1_qn), .reset(Clear));  // open: preset
endmodule

module Instruction_Cache (
  input  [31:0] Data_from_RAM_0,
  input  [31:0] Data_from_RAM_2,
  input  [31:0] Data_from_RAM_1,
  input  [31:0] Data_from_RAM_3,
  input  [31:0] Address,
  input  Read,
  input  Clock,
  input  Clear,
  input  RAM_read_finish,
  input  RAM_Write,
  output [31:0] Data_Out_of_Cache,
  output Miss_Hit
);

  wire and_9_out, and_10_out, and_11_out, and_12_out, and_13_out, and_14_out, and_15_out, and_16_out,
       and_17_out, and_18_out, and_19_out, and_20_out, and_21_out, and_22_out, and_23_out, and_24_out,
       and_33_out, and_34_out, and_35_out, and_36_out, and_37_out, and_38_out, and_39_out, and_40_out,
       and_41_out, and_42_out, and_43_out, and_44_out, and_45_out, and_46_out, and_47_out, and_48_out, ClV0,
       ClV1, ClV2, ClV3, ClV4, ClV5, ClV6, ClV7, ClV8, ClV9, ClV10, ClV11, ClV12, ClV13, ClV14, ClV15, E0,
       E1, E2, E3, E4, E5, E6, E7, E8, E9, E10, E11, E12, E13, E14, E15, Line_0, Line_1, Line_2, Line_3,
       Line_4, Line_5, Line_6, Line_7, Line_8, Line_9, Line_10, Line_11, Line_12, Line_13, Line_14, Line_15,
       Match_Data0, Match_Data1, Match_Data2, Match_Data3, Match_Data4, Match_Data5, Match_Data6,
       Match_Data7, Match_Data8, Match_Data9, Match_Data10, Match_Data11, Match_Data12, Match_Data13,
       Match_Data14, Match_Data15, Match_Tag0, Match_Tag1, Match_Tag2, Match_Tag3, Match_Tag4, Match_Tag5,
       Match_Tag6, Match_Tag7, Match_Tag8, Match_Tag9, Match_Tag10, Match_Tag11, Match_Tag12, Match_Tag13,
       Match_Tag14, Match_Tag15, or_17_out, V0, V1, V2, V3, V4, V5, V6, V7, V8, V9, V10, V11, V12, V13, V14,
       V15;
  wire [25:0] Tag, Tag0, Tag1, Tag2, Tag3, Tag4, Tag5, Tag6, Tag7, Tag8, Tag9, Tag10, Tag11, Tag12, Tag13,
       Tag14, Tag15;
  wire [31:0] _000000, _000001, _000010, _000011, _000100, _000101, _000110, _000111, _001000, _001001,
       _001010, _001011, _001100, _001101, _001110, _001111, _010000, _010001, _010010, _010011, _010100,
       _010101, _010110, _010111, _011000, _011001, _011010, _011011, _011100, _011101, _011110, _011111,
       _100000, _100001, _100010, _100011, _100100, _100101, _100110, _100111, _101000, _101001, _101010,
       _101011, _101100, _101101, _101110, _101111, _110000, _110001, _110010, _110011, _110100, _110101,
       _110110, _110111, _111000, _111001, _111010, _111011, _111100, _111101, _111110, _111111, Out_00,
       Out_01, Out_10, Out_11;

  and and_1 (Match_Data0, Match_Tag0, Line_0);
  and and_2 (Match_Data1, Match_Tag1, Line_1);
  and and_3 (Match_Data2, Match_Tag2, Line_2);
  and and_4 (Match_Data3, Match_Tag3, Line_3);
  and and_5 (Match_Data4, Match_Tag4, Line_4);
  and and_6 (Match_Data5, Match_Tag5, Line_5);
  and and_7 (Match_Data6, Match_Tag6, Line_6);
  and and_8 (Match_Data7, Match_Tag7, Line_7);
  assign Tag = {{2{Address[31]}}, Address[31:8]};  // Bit_Extender bit_extender_1
  and and_9 (and_9_out, Match_Data0, RAM_Write);
  and and_10 (and_10_out, Match_Data1, RAM_Write);
  and and_11 (and_11_out, Match_Data2, RAM_Write);
  and and_12 (and_12_out, Match_Data3, RAM_Write);
  and and_13 (and_13_out, Match_Data4, RAM_Write);
  and and_14 (and_14_out, Match_Data5, RAM_Write);
  and and_15 (and_15_out, Match_Data6, RAM_Write);
  and and_16 (and_16_out, Match_Data7, RAM_Write);
  and and_17 (and_17_out, Match_Data8, RAM_Write);
  and and_18 (and_18_out, Match_Data9, RAM_Write);
  and and_19 (and_19_out, Match_Data10, RAM_Write);
  and and_20 (and_20_out, Match_Data11, RAM_Write);
  and and_21 (and_21_out, Match_Data12, RAM_Write);
  and and_22 (and_22_out, Match_Data13, RAM_Write);
  and and_23 (and_23_out, Match_Data14, RAM_Write);
  and and_24 (and_24_out, Match_Data15, RAM_Write);
  and and_25 (Match_Data8, Match_Tag8, Line_8);
  and and_26 (Match_Data9, Match_Tag9, Line_9);
  and and_27 (Match_Data10, Match_Tag10, Line_10);
  and and_28 (Match_Data11, Match_Tag11, Line_11);
  and and_29 (Match_Data12, Match_Tag12, Line_12);
  and and_30 (Match_Data13, Match_Tag13, Line_13);
  and and_31 (Match_Data14, Match_Tag14, Line_14);
  and and_32 (Match_Data15, Match_Tag15, Line_15);
  or or_1 (ClV0, Clear, and_9_out);
  or or_2 (ClV1, Clear, and_10_out);
  or or_3 (ClV2, Clear, and_11_out);
  or or_4 (ClV3, Clear, and_12_out);
  or or_5 (ClV4, Clear, and_13_out);
  or or_6 (ClV5, Clear, and_14_out);
  or or_7 (ClV6, Clear, and_15_out);
  or or_8 (ClV7, Clear, and_16_out);
  or or_9 (ClV8, Clear, and_17_out);
  or or_10 (ClV9, Clear, and_18_out);
  or or_11 (ClV10, Clear, and_19_out);
  or or_12 (ClV11, Clear, and_20_out);
  or or_13 (ClV12, Clear, and_21_out);
  or or_14 (ClV13, Clear, and_22_out);
  or or_15 (ClV14, Clear, and_23_out);
  or or_16 (ClV15, Clear, and_24_out);
  Comparator #(.width(26)) comparator_1 (.a(Tag), .b(Tag0), .eq(Match_Tag0));  // open: gt, lt
  Comparator #(.width(26)) comparator_2 (.a(Tag), .b(Tag1), .eq(Match_Tag1));  // open: gt, lt
  Comparator #(.width(26)) comparator_3 (.a(Tag), .b(Tag2), .eq(Match_Tag2));  // open: gt, lt
  Comparator #(.width(26)) comparator_4 (.a(Tag), .b(Tag3), .eq(Match_Tag3));  // open: gt, lt
  Comparator #(.width(26)) comparator_5 (.a(Tag), .b(Tag4), .eq(Match_Tag4));  // open: gt, lt
  Comparator #(.width(26)) comparator_6 (.a(Tag), .b(Tag5), .eq(Match_Tag5));  // open: gt, lt
  Comparator #(.width(26)) comparator_7 (.a(Tag), .b(Tag6), .eq(Match_Tag6));  // open: gt, lt
  Comparator #(.width(26)) comparator_8 (.a(Tag), .b(Tag7), .eq(Match_Tag7));  // open: gt, lt
  Comparator #(.width(26)) comparator_9 (.a(Tag), .b(Tag8), .eq(Match_Tag8));  // open: gt, lt
  Comparator #(.width(26)) comparator_10 (.a(Tag), .b(Tag9), .eq(Match_Tag9));  // open: gt, lt
  Comparator #(.width(26)) comparator_11 (.a(Tag), .b(Tag10), .eq(Match_Tag10));  // open: gt, lt
  Comparator #(.width(26)) comparator_12 (.a(Tag), .b(Tag11), .eq(Match_Tag11));  // open: gt, lt
  Comparator #(.width(26)) comparator_13 (.a(Tag), .b(Tag12), .eq(Match_Tag12));  // open: gt, lt
  Comparator #(.width(26)) comparator_14 (.a(Tag), .b(Tag13), .eq(Match_Tag13));  // open: gt, lt
  Comparator #(.width(26)) comparator_15 (.a(Tag), .b(Tag14), .eq(Match_Tag14));  // open: gt, lt
  Comparator #(.width(26)) comparator_16 (.a(Tag), .b(Tag15), .eq(Match_Tag15));  // open: gt, lt
  Decoder #(.select(4), .enable("false")) decoder_1 (
    .out0(Line_0), .out1(Line_1), .out2(Line_2), .out3(Line_3), .out4(Line_4), .out5(Line_5), .out6(Line_6),
    .out7(Line_7), .out8(Line_8), .out9(Line_9), .out10(Line_10), .out11(Line_11), .out12(Line_12),
    .out13(Line_13), .out14(Line_14), .out15(Line_15), .sel(Address[7:4]));
  and and_33 (and_33_out, Match_Data0, V0);
  and and_34 (and_34_out, Match_Data8, V8);
  and and_35 (and_35_out, Match_Data1, V1);
  and and_36 (and_36_out, Match_Data9, V9);
  and and_37 (and_37_out, Match_Data2, V2);
  and and_38 (and_38_out, Match_Data10, V10);
  and and_39 (and_39_out, Match_Data3, V3);
  and and_40 (and_40_out, Match_Data11, V11);
  and and_41 (and_41_out, Match_Data4, V4);
  and and_42 (and_42_out, Match_Data12, V12);
  and and_43 (and_43_out, Match_Data5, V5);
  and and_44 (and_44_out, Match_Data13, V13);
  and and_45 (and_45_out, Match_Data6, V6);
  and and_46 (and_46_out, Match_Data14, V14);
  and and_47 (and_47_out, Match_Data7, V7);
  and and_48 (and_48_out, Match_Data15, V15);
  Register #(.width(26)) u_Tag0 (.D(Tag), .en(E0), .Q(Tag0), .clk(Clock), .clr(Clear));
  Register #(.width(26)) u_Tag1 (.D(Tag), .en(E1), .Q(Tag1), .clk(Clock), .clr(Clear));
  Register #(.width(26)) u_Tag2 (.D(Tag), .en(E2), .Q(Tag2), .clk(Clock), .clr(Clear));
  Register #(.width(26)) u_Tag3 (.D(Tag), .en(E3), .Q(Tag3), .clk(Clock), .clr(Clear));
  Register #(.width(26)) u_Tag4 (.D(Tag), .en(E4), .Q(Tag4), .clk(Clock), .clr(Clear));
  Register #(.width(26)) u_Tag5 (.D(Tag), .en(E5), .Q(Tag5), .clk(Clock), .clr(Clear));
  Register #(.width(26)) u_Tag6 (.D(Tag), .en(E6), .Q(Tag6), .clk(Clock), .clr(Clear));
  Register #(.width(26)) u_Tag7 (.D(Tag), .en(E7), .Q(Tag7), .clk(Clock), .clr(Clear));
  or or_17 (or_17_out, and_33_out, and_34_out, and_35_out, and_36_out, and_37_out, and_38_out, and_39_out, and_40_out, and_41_out, and_42_out, and_43_out, and_44_out, and_45_out, and_46_out, and_47_out, and_48_out);
  and and_49 (Miss_Hit, or_17_out, Read);
  Register #(.width(26)) u_Tag8 (.D(Tag), .en(E8), .Q(Tag8), .clk(Clock), .clr(Clear));
  Register #(.width(26)) u_Tag9 (.D(Tag), .en(E9), .Q(Tag9), .clk(Clock), .clr(Clear));
  Register #(.width(26)) u_Tag10 (.D(Tag), .en(E10), .Q(Tag10), .clk(Clock), .clr(Clear));
  Register #(.width(26)) u_Tag11 (.D(Tag), .en(E11), .Q(Tag11), .clk(Clock), .clr(Clear));
  Register #(.width(26)) u_Tag12 (.D(Tag), .en(E12), .Q(Tag12), .clk(Clock), .clr(Clear));
  Register #(.width(26)) u_Tag13 (.D(Tag), .en(E13), .Q(Tag13), .clk(Clock), .clr(Clear));
  Register #(.width(26)) u_Tag14 (.D(Tag), .en(E14), .Q(Tag14), .clk(Clock), .clr(Clear));
  Register #(.width(26)) u_Tag15 (.D(Tag), .en(E15), .Q(Tag15), .clk(Clock), .clr(Clear));
  Bit_de_validez bit_de_validez_1 (.Clock(Clock), .Output(V0), .In(E0), .Clear(ClV0));
  Bit_de_validez bit_de_validez_2 (.Clock(Clock), .Output(V1), .In(E1), .Clear(ClV1));
  Bit_de_validez bit_de_validez_3 (.Clock(Clock), .Output(V2), .In(E2), .Clear(ClV2));
  Bit_de_validez bit_de_validez_4 (.Clock(Clock), .Output(V3), .In(E3), .Clear(ClV3));
  Bit_de_validez bit_de_validez_5 (.Clock(Clock), .Output(V4), .In(E4), .Clear(ClV4));
  Bit_de_validez bit_de_validez_6 (.Clock(Clock), .Output(V5), .In(E5), .Clear(ClV5));
  Bit_de_validez bit_de_validez_7 (.Clock(Clock), .Output(V6), .In(E6), .Clear(ClV6));
  Bit_de_validez bit_de_validez_8 (.Clock(Clock), .Output(V7), .In(E7), .Clear(ClV7));
  Bit_de_validez bit_de_validez_9 (.Clock(Clock), .Output(V8), .In(E8), .Clear(ClV8));
  Bit_de_validez bit_de_validez_10 (.Clock(Clock), .Output(V9), .In(E9), .Clear(ClV9));
  Bit_de_validez bit_de_validez_11 (.Clock(Clock), .Output(V10), .In(E10), .Clear(ClV10));
  Bit_de_validez bit_de_validez_12 (.Clock(Clock), .Output(V11), .In(E11), .Clear(ClV11));
  Bit_de_validez bit_de_validez_13 (.Clock(Clock), .Output(V12), .In(E12), .Clear(ClV12));
  Bit_de_validez bit_de_validez_14 (.Clock(Clock), .Output(V13), .In(E13), .Clear(ClV13));
  Bit_de_validez bit_de_validez_15 (.Clock(Clock), .Output(V14), .In(E14), .Clear(ClV14));
  Bit_de_validez bit_de_validez_16 (.Clock(Clock), .Output(V15), .In(E15), .Clear(ClV15));
  Register #(.width(32)) register_1 (.D(Data_from_RAM_3), .en(E0), .Q(_000011), .clk(Clock), .clr(Clear));
  Register #(.width(32)) register_2 (.D(Data_from_RAM_3), .en(E1), .Q(_000111), .clk(Clock), .clr(Clear));
  Register #(.width(32)) register_3 (.D(Data_from_RAM_3), .en(E2), .Q(_001011), .clk(Clock), .clr(Clear));
  Register #(.width(32)) register_4 (.D(Data_from_RAM_3), .en(E3), .Q(_001111), .clk(Clock), .clr(Clear));
  Register #(.width(32)) register_5 (.D(Data_from_RAM_3), .en(E4), .Q(_010011), .clk(Clock), .clr(Clear));
  Register #(.width(32)) register_6 (.D(Data_from_RAM_3), .en(E5), .Q(_010111), .clk(Clock), .clr(Clear));
  Register #(.width(32)) register_7 (.D(Data_from_RAM_3), .en(E6), .Q(_011011), .clk(Clock), .clr(Clear));
  Register #(.width(32)) register_8 (.D(Data_from_RAM_3), .en(E7), .Q(_011111), .clk(Clock), .clr(Clear));
  Register #(.width(32)) register_9 (.D(Data_from_RAM_3), .en(E8), .Q(_100011), .clk(Clock), .clr(Clear));
  Register #(.width(32)) register_10 (.D(Data_from_RAM_3), .en(E9), .Q(_100111), .clk(Clock), .clr(Clear));
  Register #(.width(32)) register_11 (.D(Data_from_RAM_3), .en(E10), .Q(_101011), .clk(Clock), .clr(Clear));
  Register #(.width(32)) register_12 (.D(Data_from_RAM_3), .en(E11), .Q(_101111), .clk(Clock), .clr(Clear));
  Register #(.width(32)) register_13 (.D(Data_from_RAM_3), .en(E12), .Q(_110011), .clk(Clock), .clr(Clear));
  Register #(.width(32)) register_14 (.D(Data_from_RAM_3), .en(E13), .Q(_110111), .clk(Clock), .clr(Clear));
  Register #(.width(32)) register_15 (.D(Data_from_RAM_3), .en(E14), .Q(_111011), .clk(Clock), .clr(Clear));
  Register #(.width(32)) register_16 (.D(Data_from_RAM_3), .en(E15), .Q(_111111), .clk(Clock), .clr(Clear));
  Multiplexer #(.select(2), .width(32), .enable("false")) multiplexer_1 (
    .in0(Out_00), .in1(Out_01), .in2(Out_10), .in3(Out_11), .out(Data_Out_of_Cache), .sel(Address[3:2]));
  Register #(.width(32)) register_17 (.D(Data_from_RAM_2), .en(E0), .Q(_000010), .clk(Clock), .clr(Clear));
  Register #(.width(32)) register_18 (.D(Data_from_RAM_2), .en(E1), .Q(_000110), .clk(Clock), .clr(Clear));
  Register #(.width(32)) register_19 (.D(Data_from_RAM_2), .en(E2), .Q(_001010), .clk(Clock), .clr(Clear));
  Register #(.width(32)) register_20 (.D(Data_from_RAM_2), .en(E3), .Q(_001110), .clk(Clock), .clr(Clear));
  Register #(.width(32)) register_21 (.D(Data_from_RAM_2), .en(E4), .Q(_010010), .clk(Clock), .clr(Clear));
  Register #(.width(32)) register_22 (.D(Data_from_RAM_2), .en(E5), .Q(_010110), .clk(Clock), .clr(Clear));
  Register #(.width(32)) register_23 (.D(Data_from_RAM_2), .en(E6), .Q(_011010), .clk(Clock), .clr(Clear));
  Register #(.width(32)) register_24 (.D(Data_from_RAM_2), .en(E7), .Q(_011110), .clk(Clock), .clr(Clear));
  Register #(.width(32)) register_25 (.D(Data_from_RAM_2), .en(E8), .Q(_100010), .clk(Clock), .clr(Clear));
  Register #(.width(32)) register_26 (.D(Data_from_RAM_2), .en(E9), .Q(_100110), .clk(Clock), .clr(Clear));
  Register #(.width(32)) register_27 (.D(Data_from_RAM_2), .en(E10), .Q(_101010), .clk(Clock), .clr(Clear));
  Register #(.width(32)) register_28 (.D(Data_from_RAM_2), .en(E11), .Q(_101110), .clk(Clock), .clr(Clear));
  Register #(.width(32)) register_29 (.D(Data_from_RAM_2), .en(E12), .Q(_110010), .clk(Clock), .clr(Clear));
  Register #(.width(32)) register_30 (.D(Data_from_RAM_2), .en(E13), .Q(_110110), .clk(Clock), .clr(Clear));
  Register #(.width(32)) register_31 (.D(Data_from_RAM_2), .en(E14), .Q(_111010), .clk(Clock), .clr(Clear));
  Register #(.width(32)) register_32 (.D(Data_from_RAM_2), .en(E15), .Q(_111110), .clk(Clock), .clr(Clear));
  Register #(.width(32)) register_33 (.D(Data_from_RAM_1), .en(E0), .Q(_000001), .clk(Clock), .clr(Clear));
  Register #(.width(32)) register_34 (.D(Data_from_RAM_1), .en(E1), .Q(_000101), .clk(Clock), .clr(Clear));
  Register #(.width(32)) register_35 (.D(Data_from_RAM_1), .en(E2), .Q(_001001), .clk(Clock), .clr(Clear));
  Register #(.width(32)) register_36 (.D(Data_from_RAM_1), .en(E3), .Q(_001101), .clk(Clock), .clr(Clear));
  Register #(.width(32)) register_37 (.D(Data_from_RAM_1), .en(E4), .Q(_010001), .clk(Clock), .clr(Clear));
  Register #(.width(32)) register_38 (.D(Data_from_RAM_1), .en(E5), .Q(_010101), .clk(Clock), .clr(Clear));
  Register #(.width(32)) register_39 (.D(Data_from_RAM_1), .en(E6), .Q(_011001), .clk(Clock), .clr(Clear));
  Register #(.width(32)) register_40 (.D(Data_from_RAM_1), .en(E7), .Q(_011101), .clk(Clock), .clr(Clear));
  Register #(.width(32)) register_41 (.D(Data_from_RAM_1), .en(E8), .Q(_100001), .clk(Clock), .clr(Clear));
  Register #(.width(32)) register_42 (.D(Data_from_RAM_1), .en(E9), .Q(_100101), .clk(Clock), .clr(Clear));
  Register #(.width(32)) register_43 (.D(Data_from_RAM_1), .en(E10), .Q(_101001), .clk(Clock), .clr(Clear));
  Register #(.width(32)) register_44 (.D(Data_from_RAM_1), .en(E11), .Q(_101101), .clk(Clock), .clr(Clear));
  Register #(.width(32)) register_45 (.D(Data_from_RAM_1), .en(E12), .Q(_110001), .clk(Clock), .clr(Clear));
  Register #(.width(32)) register_46 (.D(Data_from_RAM_1), .en(E13), .Q(_110101), .clk(Clock), .clr(Clear));
  Register #(.width(32)) register_47 (.D(Data_from_RAM_1), .en(E14), .Q(_111001), .clk(Clock), .clr(Clear));
  Register #(.width(32)) register_48 (.D(Data_from_RAM_1), .en(E15), .Q(_111101), .clk(Clock), .clr(Clear));
  and and_50 (E0, RAM_read_finish, Line_0);
  and and_51 (E1, RAM_read_finish, Line_1);
  and and_52 (E2, RAM_read_finish, Line_2);
  and and_53 (E3, RAM_read_finish, Line_3);
  and and_54 (E4, RAM_read_finish, Line_4);
  and and_55 (E5, RAM_read_finish, Line_5);
  and and_56 (E6, RAM_read_finish, Line_6);
  and and_57 (E7, RAM_read_finish, Line_7);
  Register #(.width(32)) register_49 (.D(Data_from_RAM_0), .en(E0), .Q(_000000), .clk(Clock), .clr(Clear));
  Register #(.width(32)) register_50 (.D(Data_from_RAM_0), .en(E1), .Q(_000100), .clk(Clock), .clr(Clear));
  Register #(.width(32)) register_51 (.D(Data_from_RAM_0), .en(E2), .Q(_001000), .clk(Clock), .clr(Clear));
  Register #(.width(32)) register_52 (.D(Data_from_RAM_0), .en(E3), .Q(_001100), .clk(Clock), .clr(Clear));
  Register #(.width(32)) register_53 (.D(Data_from_RAM_0), .en(E4), .Q(_010000), .clk(Clock), .clr(Clear));
  Register #(.width(32)) register_54 (.D(Data_from_RAM_0), .en(E5), .Q(_010100), .clk(Clock), .clr(Clear));
  Register #(.width(32)) register_55 (.D(Data_from_RAM_0), .en(E6), .Q(_011000), .clk(Clock), .clr(Clear));
  Register #(.width(32)) register_56 (.D(Data_from_RAM_0), .en(E7), .Q(_011100), .clk(Clock), .clr(Clear));
  Register #(.width(32)) register_57 (.D(Data_from_RAM_0), .en(E8), .Q(_100000), .clk(Clock), .clr(Clear));
  Register #(.width(32)) register_58 (.D(Data_from_RAM_0), .en(E9), .Q(_100100), .clk(Clock), .clr(Clear));
  Register #(.width(32)) register_59 (.D(Data_from_RAM_0), .en(E10), .Q(_101000), .clk(Clock), .clr(Clear));
  Register #(.width(32)) register_60 (.D(Data_from_RAM_0), .en(E11), .Q(_101100), .clk(Clock), .clr(Clear));
  Register #(.width(32)) register_61 (.D(Data_from_RAM_0), .en(E12), .Q(_110000), .clk(Clock), .clr(Clear));
  Register #(.width(32)) register_62 (.D(Data_from_RAM_0), .en(E13), .Q(_110100), .clk(Clock), .clr(Clear));
  Register #(.width(32)) register_63 (.D(Data_from_RAM_0), .en(E14), .Q(_111000), .clk(Clock), .clr(Clear));
  Register #(.width(32)) register_64 (.D(Data_from_RAM_0), .en(E15), .Q(_111100), .clk(Clock), .clr(Clear));
  and and_58 (E8, RAM_read_finish, Line_8);
  and and_59 (E9, RAM_read_finish, Line_9);
  and and_60 (E10, RAM_read_finish, Line_10);
  and and_61 (E11, RAM_read_finish, Line_11);
  and and_62 (E12, RAM_read_finish, Line_12);
  and and_63 (E13, RAM_read_finish, Line_13);
  and and_64 (E14, RAM_read_finish, Line_14);
  and and_65 (E15, RAM_read_finish, Line_15);
  Multiplexer #(.select(4), .width(32)) multiplexer_2 (
    .in0(_000000), .in1(_000100), .in2(_001000), .in3(_001100), .in4(_010000), .in5(_010100), .in6(_011000),
    .in7(_011100), .in8(_100000), .in9(_100100), .in10(_101000), .in11(_101100), .in12(_110000),
    .in13(_110100), .in14(_111000), .in15(_111100), .out(Out_00), .sel(Address[7:4]), .en(Miss_Hit));
  Multiplexer #(.select(4), .width(32)) multiplexer_3 (
    .in0(_000001), .in1(_000101), .in2(_001001), .in3(_001101), .in4(_010001), .in5(_010101), .in6(_011001),
    .in7(_011101), .in8(_100001), .in9(_100101), .in10(_101001), .in11(_101101), .in12(_110001),
    .in13(_110101), .in14(_111001), .in15(_111101), .out(Out_01), .sel(Address[7:4]), .en(Miss_Hit));
  Multiplexer #(.select(4), .width(32)) multiplexer_4 (
    .in0(_000010), .in1(_000110), .in2(_001010), .in3(_001110), .in4(_010010), .in5(_010110), .in6(_011010),
    .in7(_011110), .in8(_100010), .in9(_100110), .in10(_101010), .in11(_101110), .in12(_110010),
    .in13(_110110), .in14(_111010), .in15(_111110), .out(Out_10), .sel(Address[7:4]), .en(Miss_Hit));
  Multiplexer #(.select(4), .width(32)) multiplexer_5 (
    .in0(_000011), .in1(_000111), .in2(_001011), .in3(_001111), .in4(_010011), .in5(_010111), .in6(_011011),
    .in7(_011111), .in8(_100011), .in9(_100111), .in10(_101011), .in11(_101111), .in12(_110011),
    .in13(_110111), .in14(_111011), .in15(_111111), .out(Out_11), .sel(Address[7:4]), .en(Miss_Hit));

  // Other names for the same wires on the sheet: Offset[1:0] = Address[3:2]; Index[3:0] = Address[7:4];
  //   Data_to_cpu[31:0] = Data_Out_of_Cache; Hit = Miss_Hit; In_00[31:0] = Data_from_RAM_0;
  //   In_01[31:0] = Data_from_RAM_1; In_10[31:0] = Data_from_RAM_2; In_11[31:0] = Data_from_RAM_3; T0 = E0; T1 = E1;
  //   T2 = E2; T3 = E3; T4 = E4; T5 = E5; T6 = E6; T7 = E7; T8 = E8; T9 = E9; T10 = E10; T11 = E11; T12 = E12;
  //   T13 = E13; T14 = E14; T15 = E15
endmodule

// Instruction Memory
module Instruction_Memory_Cache (
  input  Clock,
  input  Reset,
  input  Get,
  input  [31:0] Address,
  input  [3:0] Read_Time,
  input  [31:0] RO0,
  input  [31:0] RO2,
  input  [31:0] RO1,
  input  [31:0] RO3,
  input  Write_RAM,
  input  Halt,
  output Chip_Select,
  output Ready,
  output [15:0] RAM_Address,
  output Cache_on_work,
  output [31:0] Data_output
);

  wire CS1, CS2, d_ff_3_q, Miss_Hit, nStop, or_2_out, or_3_out, or_4_out, or_5_out, out_sec, RAM_read_finish,
       Reset_t, Stop, timer_1_ready;
  wire [1:0] Output_Selector;
  wire [3:0] Mask;
  wire [31:0] Data_from_Cache, Hits_q, instruction_cache_1_data_out_of_cache, Inversor_2_data_out,
       Inversor_3_data_out, Inversor_4_data_out, Inversor_5_data_out, Inversor_data_out, Misses_q,
       multiplexer_1_out, RAM_OUTPUT_0, RAM_OUTPUT_1, RAM_OUTPUT_2, RAM_OUTPUT_3;

  or or_1 (Reset_t, RAM_read_finish, Reset);
  Register #(.width(32)) register_1 (.D(RO0), .en(CS2), .Q(RAM_OUTPUT_0), .clk(Clock));  // open: clr
  Register #(.width(32)) register_2 (.D(RO1), .en(CS2), .Q(RAM_OUTPUT_1), .clk(Clock));  // open: clr
  Address_Separator Address_separator (
    .Address(Address), .Output_selector(Output_Selector), .Mask(Mask), .RAM_Address(RAM_Address));
  Inversor Inversor (.Data_In(RAM_OUTPUT_2), .Data_Out(Inversor_data_out));
  Inversor Inversor_2 (.Data_In(RAM_OUTPUT_1), .Data_Out(Inversor_2_data_out));
  Inversor Inversor_3 (.Data_In(RAM_OUTPUT_0), .Data_Out(Inversor_3_data_out));
  Register #(.width(32)) register_3 (.D(RO2), .en(CS2), .Q(RAM_OUTPUT_2), .clk(Clock));  // open: clr
  Register #(.width(32)) register_4 (.D(RO3), .en(CS2), .Q(RAM_OUTPUT_3), .clk(Clock));  // open: clr
  Inversor Inversor_4 (.Data_In(RAM_OUTPUT_3), .Data_Out(Inversor_4_data_out));
  or or_2 (or_2_out, Get, timer_1_ready);
  Register #(.width(32), .trigger("high")) register_5 (
    .D(instruction_cache_1_data_out_of_cache), .en(Miss_Hit), .Q(Data_from_Cache), .clk(Clock));  // open: clr
  Instruction_Cache instruction_cache_1 (
    .Data_from_RAM_0(Inversor_3_data_out), .Data_from_RAM_2(Inversor_data_out),
    .Data_from_RAM_1(Inversor_2_data_out), .Data_from_RAM_3(Inversor_4_data_out), .Address(Address),
    .Read(Get), .Clock(Clock), .Clear(Reset), .RAM_read_finish(RAM_read_finish),
    .Data_Out_of_Cache(instruction_cache_1_data_out_of_cache), .Miss_Hit(Miss_Hit), .RAM_Write(Write_RAM));
  or or_3 (or_3_out, CS1, CS2);
  D_Flip_Flop #(.trigger("falling")) d_ff_1 (
    .clk(Clock), .D(Get), .Q(CS1), .en(or_2_out), .reset(Miss_Hit));  // open: Qn, preset
  and and_1 (Chip_Select, or_3_out, nStop);
  // Probe on Data_from_Cache
  Timer timer_1 (.Time(Read_Time), .Clock(Clock), .Reset(Reset_t), .Start(CS1), .Ready(timer_1_ready));
  D_Flip_Flop #(.trigger("falling")) d_ff_2 (
    .clk(Clock), .D(timer_1_ready), .Q(CS2), .reset(d_ff_3_q));  // open: Qn, preset, en
  Multiplexer #(.select(2), .width(32), .disabled(0), .enable("false")) multiplexer_1 (
    .in0(RAM_OUTPUT_0), .in1(RAM_OUTPUT_1), .in2(RAM_OUTPUT_2), .in3(RAM_OUTPUT_3), .out(multiplexer_1_out),
    .sel(Output_Selector));
  Inversor Inversor_5 (.Data_In(multiplexer_1_out), .Data_Out(Inversor_5_data_out));
  // Probe on Output_Selector
  and and_2 (Ready, nStop, or_4_out);
  or or_4 (or_4_out, out_sec, d_ff_3_q);
  D_Flip_Flop #(.trigger("falling")) d_ff_3 (.clk(Clock), .D(CS2), .Q(d_ff_3_q));  // open: Qn, preset, en, reset
  Multiplexer #(.width(32), .disabled(0), .enable("false")) multiplexer_2 (
    .in0(Inversor_5_data_out), .in1(Data_from_Cache), .out(Data_output), .sel(out_sec));
  D_Flip_Flop #(.trigger("falling")) d_ff_4 (
    .clk(Clock), .D(Miss_Hit), .Q(Cache_on_work));  // open: Qn, preset, en, reset
  and and_3 (RAM_read_finish, ~Miss_Hit, d_ff_3_q);  // AND_Gate
  Counter #(.width(32), .max('hffffffff)) Misses (
    .load(Stop), .D(Misses_q), .count(nStop), .Q(Misses_q), .clk(d_ff_3_q));  // open: carry, clr
  // Probe on Misses_q
  D_Flip_Flop #(.trigger("falling")) d_ff_5 (
    .clk(Clock), .D(Cache_on_work), .Q(out_sec));  // open: Qn, preset, en, reset
  or or_5 (or_5_out, Stop, Halt);
  Counter #(.width(32), .max('hffffffff)) Hits (
    .load(Stop), .D(Hits_q), .count(nStop), .Q(Hits_q), .clk(out_sec));  // open: carry, clr
  D_Flip_Flop #(.trigger("falling")) d_ff_6 (
    .clk(Clock), .D(or_5_out), .Q(Stop), .Qn(nStop));  // open: preset, en, reset
  // Probe on Hits_q

  // Other names for the same wires on the sheet: Addr[31:0] = Address; Clck = Clock; Clr = Reset
endmodule
